// Logisim project p1.circ as structural Verilog: 1 circuit, main circuit main
module main (
  input  A,
  input  B
);

  wire transistor_1_out, transistor_2_out;

  Transistor transistor_1 (.in(1'b1), .out(transistor_1_out), .gate(A));
  Transistor transistor_2 (.in(transistor_1_out), .out(transistor_2_out), .gate(B));
  Transistor #(.\type ("n")) transistor_3 (.in(1'b0), .out(transistor_2_out), .gate(B));
  Transistor #(.\type ("n")) transistor_4 (.in(1'b0), .out(transistor_2_out), .gate(A));
  // Probe on transistor_2_out

  // Notes on the sheet:
  //   NOR GATE
endmodule
