// Logisim project p4.circ as structural Verilog: 1 circuit, main circuit main
module main (
  input  A,
  input  B,
  input  C
);

  wire transistor_1_out, transistor_2_out, transistor_3_out;

  Transistor transistor_1 (.in(1'b0), .out(transistor_1_out), .gate(A));
  Transistor #(.\type ("n")) transistor_2 (.in(1'b1), .out(transistor_2_out), .gate(A));
  Transistor #(.\type ("n")) transistor_3 (.in(transistor_2_out), .out(transistor_3_out), .gate(B));
  Transistor #(.\type ("n")) transistor_4 (.in(transistor_3_out), .out(transistor_1_out), .gate(C));
  Transistor transistor_5 (.in(1'b0), .out(transistor_1_out), .gate(B));
  Transistor transistor_6 (.in(1'b0), .out(transistor_1_out), .gate(C));
  // Probe on transistor_1_out

  // Notes on the sheet:
  //   AND GATE
endmodule
