// Logisim project p5.circ as structural Verilog: 1 circuit, main circuit main
module main (
  input  A,
  input  B,
  input  C,
  input  D
);

  wire transistor_1_out, transistor_6_out, transistor_7_out, transistor_8_out;

  Transistor #(.\type ("n")) transistor_1 (.in(1'b1), .out(transistor_1_out), .gate(A));
  Transistor #(.\type ("n")) transistor_2 (.in(1'b1), .out(transistor_1_out), .gate(B));
  Transistor #(.\type ("n")) transistor_3 (.in(1'b1), .out(transistor_1_out), .gate(C));
  Transistor #(.\type ("n")) transistor_4 (.in(1'b1), .out(transistor_1_out), .gate(D));
  Transistor transistor_5 (.in(transistor_6_out), .out(transistor_1_out), .gate(D));
  Transistor transistor_6 (.in(transistor_7_out), .out(transistor_6_out), .gate(C));
  Transistor transistor_7 (.in(transistor_8_out), .out(transistor_7_out), .gate(B));
  Transistor transistor_8 (.in(1'b0), .out(transistor_8_out), .gate(A));
  // Probe on transistor_1_out

  // Notes on the sheet:
  //   OR GATE
endmodule
