// Logisim project p6.circ as structural Verilog: 1 circuit, main circuit main
module main (
  input  A,
  input  B
);

  wire transistor_1_out, transistor_3_out;

  Transistor transistor_1 (.in(1'b1), .out(transistor_1_out), .gate(A));
  Transistor #(.\type ("n")) transistor_2 (.in(1'b0), .out(transistor_1_out), .gate(A));
  Transistor transistor_3 (.in(transistor_1_out), .out(transistor_3_out), .gate(B));
  Transistor #(.\type ("n")) transistor_4 (.in(A), .out(transistor_3_out), .gate(B));
  // Probe on transistor_3_out

  // Notes on the sheet:
  //   XNOR GATE
endmodule
