// Logisim project p1.circ as structural Verilog: 1 circuit, main circuit main
module main (
  input  A,
  input  B,
  input  C,
  input  D,
  input  in_5,
  output out_6
);

  wire transistor_1_out, transistor_2_out, transistor_3_out;

  Transistor transistor_1 (.in(in_5), .out(transistor_1_out), .gate(A));
  Transistor transistor_2 (.in(transistor_1_out), .out(transistor_2_out), .gate(B));
  Transistor transistor_3 (.in(transistor_2_out), .out(transistor_3_out), .gate(C));
  Transistor transistor_4 (.in(transistor_3_out), .out(out_6), .gate(D));

  // Notes on the sheet:
  //   Series Structure with 4 PMOS transistor
endmodule
