// Logisim project p2.circ as structural Verilog: 1 circuit, main circuit main
module main (
  input  A,
  input  B,
  input  C,
  input  D,
  input  E,
  output out_6,
  output out_7,
  output out_8,
  output out_9
);

  wire pull_resistor_1_node, transistor_2_out, transistor_3_out, transistor_4_out, transistor_5_out,
       transistor_8_out, transistor_9_out, transistor_10_out, transistor_11_out, transistor_12_out;

  Pull_Resistor #(.pull(1)) pull_resistor_1 (.node(pull_resistor_1_node));
  Transistor #(.\type ("n")) transistor_1 (.in(transistor_2_out), .out(pull_resistor_1_node), .gate(A));
  Transistor #(.\type ("n")) transistor_2 (.in(transistor_3_out), .out(transistor_2_out), .gate(B));
  Transistor #(.\type ("n")) transistor_3 (.in(transistor_4_out), .out(transistor_3_out), .gate(C));
  Transistor #(.\type ("n")) transistor_4 (.in(transistor_5_out), .out(transistor_4_out), .gate(D));
  Transistor #(.\type ("n")) transistor_5 (.in(1'b0), .out(transistor_5_out), .gate(E));
  Pull_Resistor #(.pull(1)) pull_resistor_2 (.node(out_6));
  Transistor #(.\type ("n")) transistor_6 (.in(1'b0), .out(out_6), .gate(pull_resistor_1_node));
  Pull_Resistor #(.pull(1)) pull_resistor_3 (.node(out_8));
  Transistor #(.\type ("n")) transistor_7 (.in(transistor_8_out), .out(out_8), .gate(A));
  Transistor #(.\type ("n")) transistor_8 (.in(transistor_9_out), .out(transistor_8_out), .gate(B));
  Transistor #(.\type ("n")) transistor_9 (.in(transistor_10_out), .out(transistor_9_out), .gate(C));
  Transistor #(.\type ("n")) transistor_10 (.in(transistor_11_out), .out(transistor_10_out), .gate(D));
  Transistor #(.\type ("n")) transistor_11 (.in(1'b0), .out(transistor_11_out), .gate(E));
  Transistor #(.\type ("n")) transistor_12 (.in(1'b0), .out(transistor_12_out), .gate(A));
  Transistor #(.\type ("n")) transistor_13 (.in(1'b0), .out(out_9), .gate(A));
  Transistor #(.\type ("n")) transistor_14 (.in(1'b0), .out(transistor_12_out), .gate(B));
  Transistor #(.\type ("n")) transistor_15 (.in(1'b0), .out(out_9), .gate(B));
  Pull_Resistor #(.pull(1)) pull_resistor_4 (.node(transistor_12_out));
  Transistor #(.\type ("n")) transistor_16 (.in(1'b0), .out(transistor_12_out), .gate(C));
  Pull_Resistor #(.pull(1)) pull_resistor_5 (.node(out_9));
  Transistor #(.\type ("n")) transistor_17 (.in(1'b0), .out(out_9), .gate(C));
  Transistor #(.\type ("n")) transistor_18 (.in(1'b0), .out(transistor_12_out), .gate(D));
  Transistor #(.\type ("n")) transistor_19 (.in(1'b0), .out(out_9), .gate(D));
  Transistor #(.\type ("n")) transistor_20 (.in(1'b0), .out(transistor_12_out), .gate(E));
  Transistor #(.\type ("n")) transistor_21 (.in(1'b0), .out(out_9), .gate(E));
  Pull_Resistor #(.pull(1)) pull_resistor_6 (.node(out_7));
  Transistor #(.\type ("n")) transistor_22 (.in(1'b0), .out(out_7), .gate(transistor_12_out));

  // Notes on the sheet:
  //   AND
  //   NAND
  //   NOR
  //   OR
endmodule
