// Logisim project p3.circ as structural Verilog: 1 circuit, main circuit main
module main (
  input  A,
  input  B,
  input  C,
  input  D,
  input  E,
  output out_6
);

  wire transistor_2_out, transistor_3_out, transistor_4_out, transistor_7_out;

  Transistor #(.\type ("n")) transistor_1 (.in(transistor_2_out), .out(out_6), .gate(A));
  Transistor #(.\type ("n")) transistor_2 (.in(1'b0), .out(transistor_2_out), .gate(B));
  Transistor transistor_3 (.in(1'b1), .out(transistor_3_out), .gate(A));
  Transistor transistor_4 (.in(transistor_3_out), .out(transistor_4_out), .gate(C));
  Transistor transistor_5 (.in(transistor_4_out), .out(out_6), .gate(E));
  Transistor #(.\type ("n")) transistor_6 (.in(transistor_7_out), .out(out_6), .gate(C));
  Transistor #(.\type ("n")) transistor_7 (.in(1'b0), .out(transistor_7_out), .gate(D));
  Transistor transistor_8 (.in(1'b1), .out(transistor_3_out), .gate(B));
  Transistor transistor_9 (.in(transistor_3_out), .out(transistor_4_out), .gate(D));
  Transistor #(.\type ("n")) transistor_10 (.in(1'b0), .out(out_6), .gate(E));

  // Notes on the sheet:
  //   _________
  //   Y = AB+CD+E
endmodule
