// Logisim project p6.circ as structural Verilog: 6 circuits, main circuit main
module main (
  input  A,
  input  B,
  input  C,
  input  D,
  output Output
);

  wire and_1_out_3, or_gate_1_out_3;

  And_Gate and_1 (.A(B), .B(C), .out_3(and_1_out_3));
  Or_gate or_gate_1 (.A(A), .B(and_1_out_3), .out_3(or_gate_1_out_3));
  Or_gate or_gate_2 (.A(or_gate_1_out_3), .B(D), .out_3(Output));

  // Notes on the sheet:
  //   And Gate
  //   Y=A+BC+D
  //   Or Gate
  //   Or Gate
endmodule

module Nor_Gate (
  input  A,
  input  B,
  output out_3
);

  wire transistor_1_out;

  Transistor transistor_1 (.in(1'b1), .out(transistor_1_out), .gate(A));
  Transistor transistor_2 (.in(transistor_1_out), .out(out_3), .gate(B));
  Transistor #(.\type ("n")) transistor_3 (.in(1'b0), .out(out_3), .gate(B));
  Transistor #(.\type ("n")) transistor_4 (.in(1'b0), .out(out_3), .gate(A));

  // Notes on the sheet:
  //   NOR GATE
endmodule

module Nand_Gate (
  input  A,
  input  B,
  output out_3
);

  wire transistor_4_out;

  Transistor transistor_1 (.in(1'b1), .out(out_3), .gate(A));
  Transistor transistor_2 (.in(1'b1), .out(out_3), .gate(B));
  Transistor #(.\type ("n")) transistor_3 (.in(transistor_4_out), .out(out_3), .gate(B));
  Transistor #(.\type ("n")) transistor_4 (.in(1'b0), .out(transistor_4_out), .gate(A));

  // Notes on the sheet:
  //   NAND GATE
endmodule

module And_Gate (
  input  A,
  input  B,
  output out_3
);

  wire transistor_1_out;

  Transistor #(.\type ("n")) transistor_1 (.in(1'b1), .out(transistor_1_out), .gate(A));
  Transistor #(.\type ("n")) transistor_2 (.in(transistor_1_out), .out(out_3), .gate(B));
  Transistor transistor_3 (.in(1'b0), .out(out_3), .gate(B));
  Transistor transistor_4 (.in(1'b0), .out(out_3), .gate(A));

  // Notes on the sheet:
  //   AND GATE
endmodule

module Or_gate (
  input  A,
  input  B,
  output out_3
);

  wire transistor_4_out;

  Transistor #(.\type ("n")) transistor_1 (.in(1'b1), .out(out_3), .gate(A));
  Transistor #(.\type ("n")) transistor_2 (.in(1'b1), .out(out_3), .gate(B));
  Transistor transistor_3 (.in(transistor_4_out), .out(out_3), .gate(B));
  Transistor transistor_4 (.in(1'b0), .out(transistor_4_out), .gate(A));

  // Notes on the sheet:
  //   OR GATE
endmodule

module Xor_Gate (
  input  A,
  input  A_2,
  output out_3
);

  wire transistor_1_out;

  Transistor transistor_1 (.in(1'b1), .out(transistor_1_out), .gate(A));
  Transistor #(.\type ("n")) transistor_2 (.in(1'b0), .out(transistor_1_out), .gate(A));
  Transistor transistor_3 (.in(A), .out(out_3), .gate(A_2));
  Transistor #(.\type ("n")) transistor_4 (.in(transistor_1_out), .out(out_3), .gate(A_2));

  // Notes on the sheet:
  //   XOR GATE
endmodule
