// Logisim project Q1.circ as structural Verilog: 1 circuit, main circuit main
module main (
  input  [7:0] in_1,
  input  in_2,
  input  [7:0] in_3,
  input  [7:0] in_4,
  input  in_5,
  input  in_6,
  output [7:0] out_7,
  output [7:0] out_8
);

  wire not_1_out;

  assign out_8 = in_6 ? in_3 : 8'bz;  // Controlled_Buffer controlled_buffer_1
  not not_1 (not_1_out, in_6);
  ROM rom_1 (.addr(in_1), .data(out_7), .sel(in_2));
  RAM ram_1 (.addr(in_4), .data(out_8), .sel(in_5), .ld(not_1_out));  // open: clk, clr

  // Notes on the sheet:
  //   contents of rom_1 (hex, n*v repeats v):
  //   1 5*0 11 6*0 11 10*0 1 0 0 1 0 1 0 0 1 5*0 1 9*0 1 51 0 0 1 4*0 1 18*0 1 4*0 11 2 14*0 1 4*0 1 27*0
  //   1 1 6*0 1 0 1 25*0 1 1 1 10*0 1 14*0 1
  //   ROM
  //   Ram
endmodule
