// Logisim project Q2.circ as structural Verilog: 1 circuit, main circuit main
module main (
  input  [20:0] in_1,
  output [31:0] out_2
);

  wire decoder_1_out0, decoder_1_out1, decoder_1_out2, decoder_1_out3;
  wire [7:0] a0, a1, a2, a3, b0, b1, b2, b3, c0, c1, c2, c3, d0, d1, d2, d3;

  Decoder #(.select(2), .enable("false")) decoder_1 (
    .out0(decoder_1_out0), .out1(decoder_1_out1), .out2(decoder_1_out2), .out3(decoder_1_out3),
    .sel(in_1[20:19]));
  Multiplexer #(.select(2), .width(8), .enable("false")) multiplexer_1 (
    .in0(a0), .in1(b0), .in3(c0), .out(out_2[7:0]), .sel(in_1[20:19]));  // open: in2
  Multiplexer #(.select(2), .width(8), .enable("false")) multiplexer_2 (
    .in0(a1), .in1(b1), .in3(c1), .out(out_2[15:8]), .sel(in_1[20:19]));  // open: in2
  Multiplexer #(.select(2), .width(8), .enable("false")) multiplexer_3 (
    .in0(a2), .in1(b2), .in3(c2), .out(out_2[23:16]), .sel(in_1[20:19]));  // open: in2
  Multiplexer #(.select(2), .width(8), .enable("false")) multiplexer_4 (
    .in0(a3), .in1(b3), .in3(c3), .out(out_2[31:24]), .sel(in_1[20:19]));  // open: in2
  ROM #(.addrWidth(19)) rom_1 (.addr(in_1[18:0]), .data(a3), .sel(decoder_1_out0));
  ROM #(.addrWidth(19)) rom_2 (.addr(in_1[18:0]), .data(b3), .sel(decoder_1_out1));
  ROM #(.addrWidth(19)) rom_3 (.addr(in_1[18:0]), .data(c3), .sel(decoder_1_out2));
  ROM #(.addrWidth(19)) rom_4 (.addr(in_1[18:0]), .data(d3), .sel(decoder_1_out3));
  ROM #(.addrWidth(19)) rom_5 (.addr(in_1[18:0]), .data(a2), .sel(decoder_1_out0));
  ROM #(.addrWidth(19)) rom_6 (.addr(in_1[18:0]), .data(b2), .sel(decoder_1_out1));
  ROM #(.addrWidth(19)) rom_7 (.addr(in_1[18:0]), .data(c2), .sel(decoder_1_out2));
  ROM #(.addrWidth(19)) rom_8 (.addr(in_1[18:0]), .data(d2), .sel(decoder_1_out3));
  ROM #(.addrWidth(19)) rom_9 (.addr(in_1[18:0]), .data(a1), .sel(decoder_1_out0));
  ROM #(.addrWidth(19)) rom_10 (.addr(in_1[18:0]), .data(b1), .sel(decoder_1_out1));
  ROM #(.addrWidth(19)) rom_11 (.addr(in_1[18:0]), .data(c1), .sel(decoder_1_out2));
  ROM #(.addrWidth(19)) rom_12 (.addr(in_1[18:0]), .data(d1), .sel(decoder_1_out3));
  ROM #(.addrWidth(19)) rom_13 (.addr(in_1[18:0]), .data(a0), .sel(decoder_1_out0));
  ROM #(.addrWidth(19)) rom_14 (.addr(in_1[18:0]), .data(b0), .sel(decoder_1_out1));
  ROM #(.addrWidth(19)) rom_15 (.addr(in_1[18:0]), .data(c0), .sel(decoder_1_out2));
  ROM #(.addrWidth(19)) rom_16 (.addr(in_1[18:0]), .data(d0), .sel(decoder_1_out3));

  // Notes on the sheet:
  //   contents of rom_1 (hex, n*v repeats v):
  //   2
  //   contents of rom_2 (hex, n*v repeats v):
  //   1
  //   contents of rom_5 (hex, n*v repeats v):
  //   1
  //   contents of rom_9 (hex, n*v repeats v):
  //   3
endmodule
