// Logisim project Q3.circ as structural Verilog: 5 circuits, main circuit main
module main (
  input  CLR,
  input  [15:0] in_2,
  output [15:0] out_3,
  output [15:0] out_4,
  output [15:0] out_5,
  output [3:0] out_6,
  output [3:0] out_7,
  output [1:0] PC,
  output [3:0] out_9,
  output [15:0] IR_PC
);

  wire Buffer_Terminal, Clk, en_re, en_store, en_wr, not_1_out;
  wire [3:0] multiplexer_1_out;
  wire [15:0] multiplexer_2_out, n16x16_ram_1_output;

  Multiplexer #(.width(4), .enable("false")) multiplexer_1 (
    .in0(IR_PC[3:0]), .in1(IR_PC[11:8]), .out(multiplexer_1_out), .sel(en_store));
  Clock clock_1 (.out(Clk));
  Multiplexer #(.width(16), .enable("false")) multiplexer_2 (
    .in0(in_2), .in1(out_5), .out(multiplexer_2_out), .sel(en_store));
  Counter #(.width(2), .max('h3), .ongoal("stay")) Counter (
    .Q(PC), .clk(Clk), .clr(CLR));  // open: load, D, count, carry
  _16x16_RAM u_16x16_ram_1 (
    .READ_ADDR(multiplexer_1_out), .WRITE_VALUE(multiplexer_2_out), .RAM_CLR(CLR),
    .Buffer_Control(Buffer_Terminal), .Output(n16x16_ram_1_output));
  not not_1 (not_1_out, 1'b1);
  ROM rom_1 (.Progress_Counter(PC), .Instruction_Register(IR_PC));
  Multiplexer #(.select(2), .enable("false")) multiplexer_3 (
    .in0(1'b1), .in1(1'b1), .in2(not_1_out), .in3(1'b1), .out(Buffer_Terminal), .sel(PC));
  _16x16_Register_File u_16x16_register_file_1 (
    .Input_Terminal__16_Bit(n16x16_ram_1_output), .Writing_Address(IR_PC[11:8]), .Clock(Clk),
    .Reading_Address_1(IR_PC[7:4]), .Reading_Address_2(IR_PC[3:0]), .Clear(CLR), .Write_Enable(en_wr),
    .Read_Enable(1'b1), .Read_Value_1(out_3), .Read_Value_2(out_4));
  Decoder #(.select(4), .enable("false")) decoder_1 (
    .out0(en_wr), .out1(en_store), .out2(en_re), .sel(IR_PC[15:12]));  // open: out3, out4, out5, out6, out7, out8, out9, out10, out11, out12, out13, out14, out15
  Adder #(.width(16)) adder_1 (.a(out_3), .b(out_4), .out(out_5));  // open: cin, cout
  Hex_Digit_Display hex_digit_display_1 (.value(out_5[11:8]));  // open: dp
  Hex_Digit_Display hex_digit_display_2 (.value(out_5[15:12]));  // open: dp
  Hex_Digit_Display hex_digit_display_3 (.value(out_5[3:0]));  // open: dp
  Hex_Digit_Display hex_digit_display_4 (.value(out_5[7:4]));  // open: dp

  assign out_6 = IR_PC[7:4];
  assign out_7 = IR_PC[3:0];
  assign out_9 = IR_PC[11:8];

  // Other names for the same wires on the sheet: op2_addr[3:0] = IR_PC[3:0]; op1_addr[3:0] = IR_PC[7:4];
  //   reg_addr[3:0] = IR_PC[11:8]; Select_Operation[3:0] = IR_PC[15:12]; Output[15:0] = out_5;
  //   read_Value_1[15:0] = out_3; read_Value_2[15:0] = out_4

  // Notes on the sheet:
  //   Datapath
  //   en_read
  //   Control Unit
  //   Load
  //   Store
  //   Add
  //   Output
endmodule

// RF
module _16x16_Register_File (
  input  [15:0] Input_Terminal__16_Bit,
  input  [3:0] Writing_Address,
  input  Clock,
  input  [3:0] Reading_Address_1,
  input  [3:0] Reading_Address_2,
  input  Write_Enable,
  input  Read_Enable,
  input  Clear,
  output [15:0] Read_Value_1,
  output [15:0] Read_Value_2
);

  wire and_1_out, and_2_out, and_3_out, and_4_out, and_5_out, and_6_out, and_7_out, and_8_out, and_9_out,
       and_10_out, and_11_out, and_12_out, and_13_out, and_14_out, and_15_out, and_16_out, decoder_1_out0,
       decoder_1_out1, decoder_1_out2, decoder_1_out3, decoder_1_out4, decoder_1_out5, decoder_1_out6,
       decoder_1_out7, decoder_1_out8, decoder_1_out9, decoder_1_out10, decoder_1_out11, decoder_1_out12,
       decoder_1_out13, decoder_1_out14, decoder_1_out15;
  wire [15:0] register_1_q, register_2_q, register_3_q, register_4_q, register_5_q, register_6_q,
       register_7_q, register_8_q, register_9_q, register_10_q, register_11_q, register_12_q, register_13_q,
       register_14_q, register_15_q, register_16_q;

  Decoder #(.select(4)) decoder_1 (
    .out0(decoder_1_out0), .out1(decoder_1_out1), .out2(decoder_1_out2), .out3(decoder_1_out3),
    .out4(decoder_1_out4), .out5(decoder_1_out5), .out6(decoder_1_out6), .out7(decoder_1_out7),
    .out8(decoder_1_out8), .out9(decoder_1_out9), .out10(decoder_1_out10), .out11(decoder_1_out11),
    .out12(decoder_1_out12), .out13(decoder_1_out13), .out14(decoder_1_out14), .out15(decoder_1_out15),
    .sel(Writing_Address));  // open: en
  and and_1 (and_1_out, decoder_1_out0, Write_Enable);
  and and_2 (and_2_out, decoder_1_out1, Write_Enable);
  and and_3 (and_3_out, decoder_1_out2, Write_Enable);
  and and_4 (and_4_out, decoder_1_out3, Write_Enable);
  and and_5 (and_5_out, decoder_1_out4, Write_Enable);
  and and_6 (and_6_out, decoder_1_out5, Write_Enable);
  and and_7 (and_7_out, decoder_1_out6, Write_Enable);
  and and_8 (and_8_out, decoder_1_out7, Write_Enable);
  and and_9 (and_9_out, Write_Enable, decoder_1_out8);
  and and_10 (and_10_out, Write_Enable, decoder_1_out9);
  and and_11 (and_11_out, Write_Enable, decoder_1_out10);
  and and_12 (and_12_out, Write_Enable, decoder_1_out11);
  and and_13 (and_13_out, Write_Enable, decoder_1_out12);
  and and_14 (and_14_out, Write_Enable, decoder_1_out13);
  and and_15 (and_15_out, Write_Enable, decoder_1_out14);
  and and_16 (and_16_out, Write_Enable, decoder_1_out15);
  Register #(.width(16)) register_1 (
    .D(Input_Terminal__16_Bit), .en(and_1_out), .Q(register_1_q), .clk(Clock), .clr(Clear));
  Register #(.width(16)) register_2 (
    .D(Input_Terminal__16_Bit), .en(and_2_out), .Q(register_2_q), .clk(Clock), .clr(Clear));
  Register #(.width(16)) register_3 (
    .D(Input_Terminal__16_Bit), .en(and_3_out), .Q(register_3_q), .clk(Clock), .clr(Clear));
  Register #(.width(16)) register_4 (
    .D(Input_Terminal__16_Bit), .en(and_4_out), .Q(register_4_q), .clk(Clock), .clr(Clear));
  Register #(.width(16)) register_5 (
    .D(Input_Terminal__16_Bit), .en(and_5_out), .Q(register_5_q), .clk(Clock), .clr(Clear));
  Register #(.width(16)) register_6 (
    .D(Input_Terminal__16_Bit), .en(and_6_out), .Q(register_6_q), .clk(Clock), .clr(Clear));
  Register #(.width(16)) register_7 (
    .D(Input_Terminal__16_Bit), .en(and_7_out), .Q(register_7_q), .clk(Clock), .clr(Clear));
  Register #(.width(16)) register_8 (
    .D(Input_Terminal__16_Bit), .en(and_8_out), .Q(register_8_q), .clk(Clock), .clr(Clear));
  Register #(.width(16)) register_9 (
    .D(Input_Terminal__16_Bit), .en(and_9_out), .Q(register_9_q), .clk(Clock), .clr(Clear));
  Register #(.width(16)) register_10 (
    .D(Input_Terminal__16_Bit), .en(and_10_out), .Q(register_10_q), .clk(Clock), .clr(Clear));
  Register #(.width(16)) register_11 (
    .D(Input_Terminal__16_Bit), .en(and_11_out), .Q(register_11_q), .clk(Clock), .clr(Clear));
  Register #(.width(16)) register_12 (
    .D(Input_Terminal__16_Bit), .en(and_12_out), .Q(register_12_q), .clk(Clock), .clr(Clear));
  Register #(.width(16)) register_13 (
    .D(Input_Terminal__16_Bit), .en(and_13_out), .Q(register_13_q), .clk(Clock), .clr(Clear));
  Register #(.width(16)) register_14 (
    .D(Input_Terminal__16_Bit), .en(and_14_out), .Q(register_14_q), .clk(Clock), .clr(Clear));
  Register #(.width(16)) register_15 (
    .D(Input_Terminal__16_Bit), .en(and_15_out), .Q(register_15_q), .clk(Clock), .clr(Clear));
  Register #(.width(16)) register_16 (
    .D(Input_Terminal__16_Bit), .en(and_16_out), .Q(register_16_q), .clk(Clock), .clr(Clear));
  Multiplexer #(.select(4), .width(16)) multiplexer_1 (
    .in0(register_1_q), .in1(register_2_q), .in2(register_3_q), .in3(register_4_q), .in4(register_5_q),
    .in5(register_6_q), .in6(register_7_q), .in7(register_8_q), .in8(register_9_q), .in9(register_10_q),
    .in10(register_11_q), .in11(register_12_q), .in12(register_13_q), .in13(register_14_q),
    .in14(register_15_q), .in15(register_16_q), .out(Read_Value_1), .sel(Reading_Address_1), .en(Read_Enable));
  Multiplexer #(.select(4), .width(16)) multiplexer_2 (
    .in0(register_1_q), .in1(register_2_q), .in2(register_3_q), .in3(register_4_q), .in4(register_5_q),
    .in5(register_6_q), .in6(register_7_q), .in7(register_8_q), .in8(register_9_q), .in9(register_10_q),
    .in10(register_11_q), .in11(register_12_q), .in12(register_13_q), .in13(register_14_q),
    .in14(register_15_q), .in15(register_16_q), .out(Read_Value_2), .sel(Reading_Address_2), .en(Read_Enable));
endmodule

// ALU
module ALU_16 (
  input  [15:0] A,
  input  [15:0] B,
  input  [3:0] Select,
  output Zero_Flag,
  output [15:0] Output,
  output [15:0] Mul_Rem
);

  wire comparator_1_lt;
  wire [15:0] adder_1_out, AND, divider_1_out, divider_1_rem, multiplexer_1_out, multiplier_1_cout,
       multiplier_1_out, NAND, NOR, OR, subtractor_1_out, XNOR, XOR;

  Comparator #(.width(16), .mode("unsigned")) comparator_1 (.a(A), .b(B), .lt(comparator_1_lt));  // open: gt, eq
  Multiplexer #(.width(16)) multiplexer_1 (
    .in0(A), .in1(B), .out(multiplexer_1_out), .sel(comparator_1_lt));  // open: en
  Adder #(.width(16)) adder_1 (.a(A), .b(B), .out(adder_1_out), .cin(1'b0));  // open: cout
  Subtractor #(.width(16)) subtractor_1 (.a(A), .b(B), .out(subtractor_1_out), .bin(1'b0));  // open: bout
  Multiplier #(.width(16)) multiplier_1 (
    .a(A), .b(B), .out(multiplier_1_out), .cin({16{1'b0}}), .cout(multiplier_1_cout));
  Divider #(.width(16)) divider_1 (.a(A), .b(B), .out(divider_1_out), .upper({16{1'b0}}), .rem(divider_1_rem));
  Multiplexer #(.select(4), .width(16)) multiplexer_2 (
    .in2(adder_1_out), .in3(subtractor_1_out), .in4(multiplier_1_out), .in5(divider_1_out), .in6(AND),
    .in7(OR), .in8(XOR), .in9(NAND), .in10(NOR), .in11(XNOR), .in12(multiplexer_1_out), .sel(Select),
    .en(1'b1));  // open: in0, in1, in13, in14, in15, out
  Multiplexer #(.select(4), .width(16)) multiplexer_3 (
    .in4(multiplier_1_cout), .in5(divider_1_rem), .sel(Select), .en(1'b1));  // open: in0, in1, in2, in3, in6, in7, in8, in9, in10, in11, in12, in13, in14, in15, out
  Comparator #(.width(16)) comparator_2 (.a({16{1'b0}}), .b(Output), .eq(Zero_Flag));  // open: gt, lt
  assign AND = A & B;  // AND_Gate and_1, 16 bits wide
  assign OR = A | B;  // OR_Gate or_1, 16 bits wide
  assign XOR = A ^ B;  // XOR_Gate xor_1, 16 bits wide
  assign XNOR = ~(A ^ B);  // XNOR_Gate xnor_1, 16 bits wide
  assign NAND = ~(A & B);  // NAND_Gate nand_1, 16 bits wide
  assign NOR = ~(A | B);  // NOR_Gate nor_1, 16 bits wide
endmodule

module ROM (
  input  [1:0] Progress_Counter,
  output [15:0] Instruction_Register
);

  ROM_part #(.addrWidth(2), .dataWidth(16)) rom_1 (.addr(Progress_Counter), .data(Instruction_Register));  // open: sel
  Hex_Digit_Display hex_digit_display_1 (.value(Instruction_Register[15:12]));  // open: dp
  Hex_Digit_Display hex_digit_display_2 (.value(Instruction_Register[7:4]));  // open: dp
  Hex_Digit_Display hex_digit_display_3 (.value(Instruction_Register[11:8]));  // open: dp
  Hex_Digit_Display hex_digit_display_4 (.value(Instruction_Register[3:0]));  // open: dp

  // Notes on the sheet:
  //   0404 = 0000 0100 0000 0100 = Load r4,x,d4 
  //   2654 = 0010 0110 0101 0100 = Add r6 = r5+r4
  //   0505 = 0000 0101 0000 0101  = Load r5 , x, d5
  //   1606 = 0001 0110 0000 0110 = Store r6 in d6
  //   16 bit address units on 2^2 =4 addresses
  //   ROM Instructions in order
  //   contents of rom_1 (hex, n*v repeats v):
  //   505 404 2654 1606
endmodule

// RAM-16
module _16x16_RAM (
  input  [3:0] READ_ADDR,
  input  [15:0] WRITE_VALUE,
  input  RAM_CLR,
  input  Buffer_Control,
  output [15:0] Output
);

  wire not_1_out;

  assign Output = Buffer_Control ? WRITE_VALUE : 16'bz;  // Controlled_Buffer controlled_buffer_1
  not not_1 (not_1_out, Buffer_Control);
  RAM #(.addrWidth(4), .dataWidth(16), .bus("asynch")) ram_1 (
    .addr(READ_ADDR), .data(Output), .ld(not_1_out), .clr(RAM_CLR));  // open: sel

  // Notes on the sheet:
  //   16x16 RAM which reads from 2^4 addresses values of upto 16 bits (2^16 bits) 
  //   For read: 0
  //   For write: 1
  //   16x16 RAM
endmodule
