// Logisim project p11.circ as structural Verilog: 1 circuit, main circuit main
module main (
  input  in_1,
  input  in_2,
  input  in_3,
  input  in_4,
  input  in_5,
  output SUM_A_B_C,
  output CARRY
);

  wire not_1_out, not_2_out;

  not not_1 (not_1_out, in_4);
  p7_main main_1 (
    .i0(in_4), .i1(not_1_out), .i2(not_1_out), .i3(in_4), .i4(not_1_out), .i5(in_4), .i6(in_4),
    .i7(not_1_out), .s0(in_1), .s1(in_2), .s2(in_3), .OUTPUT(SUM_A_B_C));
  not not_2 (not_2_out, in_5);
  p7_main main_2 (
    .i0(in_5), .i1(in_5), .i2(in_5), .i3(not_2_out), .i4(in_5), .i5(not_2_out), .i6(not_2_out),
    .i7(not_2_out), .s0(in_1), .s1(in_2), .s2(in_3), .OUTPUT(CARRY));

  // Other names for the same wires on the sheet: A = in_1; B = in_2; C = in_3
endmodule
