// Logisim project p4.circ as structural Verilog: 1 circuit, main circuit main
module main (
  input  A,
  input  B,
  input  C,
  input  D,
  input  S3,
  input  S2,
  input  S1,
  input  S0,
  output Output_to_User
);

  wire and_1_out, and_2_out, and_3_out, and_4_out, not_1_out, not_2_out, not_3_out;

  not not_1 (not_1_out, S3);
  not not_2 (not_2_out, S2);
  not not_3 (not_3_out, S1);
  not not_4 (not_3_out, S0);
  and and_1 (and_1_out, A, S0, not_3_out, not_2_out, not_1_out);
  and and_2 (and_2_out, B, S1, not_3_out, not_2_out, not_1_out);
  and and_3 (and_3_out, C, not_3_out, not_3_out, S2, not_1_out);
  and and_4 (and_4_out, D, not_3_out, not_2_out, not_3_out, S3);
  or or_1 (Output_to_User, and_1_out, and_2_out, and_3_out, and_4_out);
endmodule
