// Logisim project p5.circ as structural Verilog: 1 circuit, main circuit main
module main (
  input  a3,
  input  b3,
  input  a2,
  input  b2,
  input  a1,
  input  b1,
  input  a0,
  input  b0,
  input  s0,
  output d3,
  output d2,
  output d1,
  output d0
);

  wire and_1_out, and_2_out, and_3_out, and_4_out, and_5_out, and_6_out, and_7_out, and_8_out, not_1_out;

  not not_1 (not_1_out, s0);
  and and_1 (and_1_out, a3, s0);
  and and_2 (and_2_out, b3, not_1_out);
  and and_3 (and_3_out, a2, s0);
  and and_4 (and_4_out, b2, not_1_out);
  and and_5 (and_5_out, a1, s0);
  and and_6 (and_6_out, b1, not_1_out);
  and and_7 (and_7_out, a0, s0);
  and and_8 (and_8_out, b0, not_1_out);
  or or_1 (d3, and_1_out, and_2_out);
  or or_2 (d2, and_3_out, and_4_out);
  or or_3 (d1, and_5_out, and_6_out);
  or or_4 (d0, and_7_out, and_8_out);
endmodule
