// Logisim project p8.circ as structural Verilog: 1 circuit, main circuit main
module main (
  input  i0,
  input  i1,
  input  i2,
  input  i3,
  input  i4,
  input  i5,
  input  i6,
  input  i7,
  input  i8,
  input  i9,
  input  i10,
  input  i11,
  input  i12,
  input  i13,
  input  i14,
  input  i15,
  input  s0,
  input  s1,
  input  s2,
  input  s3,
  output Output
);

  wire _0_out, _1_out, _2_out, _3_out, _4_out, _5_out, _6_out, _7_out, _8_out, _9_out, _10_out, _11_out,
       _12_out, _13_out, _14_out, _15_out, not_1_out, not_2_out, not_3_out, not_4_out;

  not not_1 (not_1_out, s0);
  not not_2 (not_2_out, s1);
  not not_3 (not_3_out, s2);
  not not_4 (not_4_out, s3);
  and _1 (_1_out, i1, not_4_out, not_3_out, not_2_out, s0);
  and _3 (_3_out, i3, not_1_out, not_2_out, s2, s3);
  and _5 (_5_out, i5, not_1_out, s1, not_3_out, s3);
  and _7 (_7_out, i7, not_1_out, s1, s2, s3);
  and _9 (_9_out, i9, s0, not_2_out, not_3_out, s3);
  and _11 (_11_out, i11, s0, not_2_out, s2, s3);
  and _13 (_13_out, i13, s0, s1, not_3_out, s3);
  and _15 (_15_out, i15, s0, s1, s2, s3);
  and _0 (_0_out, i0, not_4_out, not_3_out, not_2_out, not_1_out);
  and _2 (_2_out, i2, not_4_out, not_3_out, s1, not_1_out);
  and _4 (_4_out, i4, not_1_out, s1, not_3_out, not_4_out);
  and _6 (_6_out, i6, not_1_out, s1, s2, not_4_out);
  and _8 (_8_out, i8, s0, not_2_out, not_3_out, not_4_out);
  and _10 (_10_out, i10, s0, not_2_out, s2, not_4_out);
  and _12 (_12_out, i12, s0, s1, not_3_out, not_4_out);
  and _14 (_14_out, i14, s0, s1, s2, not_4_out);
  or or_1 (Output, _0_out, _1_out, _2_out, _3_out, _4_out, _5_out, _6_out, _7_out, _8_out, _9_out, _10_out, _11_out, _12_out, _13_out, _14_out, _15_out);
endmodule
