// Logisim project p9.circ as structural Verilog: 3 circuits, main circuit main
module main (
  input  b0,
  input  a0,
  input  a1,
  input  b1,
  output S0,
  output S1,
  output Carry
);

  wire half_adder_1_carry;

  Half_Adder half_adder_1 (.B(a0), .A(b0), .SUM(S0), .CARRY(half_adder_1_carry));
  Full_Adder full_adder_1 (.A(half_adder_1_carry), .B(a1), .C(b1), .SUM(S1), .CARRY(Carry));

  // Notes on the sheet:
  //   Half Adder
  //   Full Adder
endmodule

module Half_Adder (
  input  B,
  input  A,
  output SUM,
  output CARRY
);

  xor xor_1 (SUM, B, A);
  and and_1 (CARRY, B, A);
endmodule

module Full_Adder (
  input  A,
  input  B,
  input  C,
  output SUM,
  output CARRY
);

  wire and_1_out, and_2_out, xor_1_out;

  xor xor_1 (xor_1_out, A, B);
  and and_1 (and_1_out, xor_1_out, C);
  and and_2 (and_2_out, A, B);
  xor xor_2 (SUM, xor_1_out, C);
  or or_1 (CARRY, and_1_out, and_2_out);
endmodule
