// Logisim project p1.circ as structural Verilog: 2 circuits, main circuit main
module main (
  input  Input_Constant_0,
  input  [7:0] in_2,
  input  [7:0] in_3,
  output [7:0] out_4,
  output Carry
);

  wire full_adder_1_carry, full_adder_2_carry, full_adder_3_carry, full_adder_4_carry, full_adder_5_carry,
       full_adder_6_carry, full_adder_7_carry, xor_1_out, xor_2_out, xor_3_out, xor_4_out, xor_5_out,
       xor_6_out, xor_7_out, xor_8_out;

  xor xor_1 (xor_1_out, in_3[0], Input_Constant_0);
  xor xor_2 (xor_2_out, in_3[1], Input_Constant_0);
  xor xor_3 (xor_3_out, in_3[2], Input_Constant_0);
  xor xor_4 (xor_4_out, in_3[3], Input_Constant_0);
  xor xor_5 (xor_5_out, in_3[4], Input_Constant_0);
  xor xor_6 (xor_6_out, in_3[5], Input_Constant_0);
  xor xor_7 (xor_7_out, in_3[6], Input_Constant_0);
  xor xor_8 (xor_8_out, in_3[7], Input_Constant_0);
  Full_Adder full_adder_1 (
    .a(in_2[0]), .b(xor_1_out), .Input(Input_Constant_0), .Carry(full_adder_1_carry), .S(out_4[0]));
  Full_Adder full_adder_2 (
    .a(in_2[1]), .b(xor_2_out), .Input(full_adder_1_carry), .Carry(full_adder_2_carry), .S(out_4[1]));
  Full_Adder full_adder_3 (
    .a(in_2[2]), .b(xor_3_out), .Input(full_adder_2_carry), .Carry(full_adder_3_carry), .S(out_4[2]));
  Full_Adder full_adder_4 (
    .a(in_2[3]), .b(xor_4_out), .Input(full_adder_3_carry), .Carry(full_adder_4_carry), .S(out_4[3]));
  Full_Adder full_adder_5 (
    .a(in_2[4]), .b(xor_5_out), .Input(full_adder_4_carry), .Carry(full_adder_5_carry), .S(out_4[4]));
  Full_Adder full_adder_6 (
    .a(in_2[5]), .b(xor_6_out), .Input(full_adder_5_carry), .Carry(full_adder_6_carry), .S(out_4[5]));
  Full_Adder full_adder_7 (
    .a(in_2[6]), .b(xor_7_out), .Input(full_adder_6_carry), .Carry(full_adder_7_carry), .S(out_4[6]));
  Full_Adder full_adder_8 (.a(in_2[7]), .b(xor_8_out), .Input(full_adder_7_carry), .Carry(Carry), .S(out_4[7]));

  // Notes on the sheet:
  //   A
  //   B
  //   Output
endmodule

module Full_Adder (
  input  Input,
  input  a,
  input  b,
  output S,
  output Carry
);

  wire and_1_out, and_2_out, xor_1_out;

  and and_1 (and_1_out, a, b);
  or or_1 (Carry, and_1_out, and_2_out);
  xor xor_1 (xor_1_out, a, b);
  and and_2 (and_2_out, xor_1_out, Input);
  xor xor_2 (S, xor_1_out, Input);
endmodule
