// Logisim project p2.circ as structural Verilog: 3 circuits, main circuit main
module main (
  input  Control,
  input  [7:0] in_2,
  input  [7:0] in_3,
  output [7:0] out_4,
  output OVERFLOW
);

  wire ic_7483_1_carry_out, ic_7483_2_carry_out, xor_1_out, xor_2_out;

  ic_7483 ic_7483_1 (
    .A0(in_2[0]), .B0(in_3[0]), .A1(in_2[1]), .B1(in_3[1]), .A2(in_2[2]), .B2(in_3[2]), .A3(in_2[3]),
    .B3(in_3[3]), .Control(Control), .Carry_Out(ic_7483_1_carry_out), .S0(out_4[0]), .S1(out_4[1]),
    .S2(out_4[2]), .S3(out_4[3]));
  ic_7483 ic_7483_2 (
    .A0(in_2[4]), .B0(in_3[4]), .A1(in_2[5]), .B1(in_3[5]), .A2(in_2[6]), .B2(in_3[6]), .A3(in_2[7]),
    .B3(in_3[7]), .Control(ic_7483_1_carry_out), .Carry_Out(ic_7483_2_carry_out), .S0(out_4[4]),
    .S1(out_4[5]), .S2(out_4[6]), .S3(out_4[7]));
  xor xor_1 (xor_1_out, in_3[7], in_2[7]);
  xor xor_2 (xor_2_out, out_4[7], ic_7483_2_carry_out);
  xor xor_3 (OVERFLOW, xor_2_out, xor_1_out);

  // Notes on the sheet:
  //   A
  //   B
  //   0  Add
  //   1  Subtract
  //   OUTPUT
endmodule

module ic_7483 (
  input  Control,
  input  A0,
  input  B0,
  input  A1,
  input  B1,
  input  A2,
  input  B2,
  input  A3,
  input  B3,
  output S0,
  output S1,
  output S2,
  output S3,
  output Carry_Out
);

  wire single_bit_adder_1_carry, single_bit_adder_2_carry, single_bit_adder_3_carry, xor_1_out, xor_2_out,
       xor_3_out, xor_4_out;

  xor xor_1 (xor_1_out, B0, Control);
  xor xor_2 (xor_2_out, B1, Control);
  xor xor_3 (xor_3_out, B2, Control);
  xor xor_4 (xor_4_out, B3, Control);
  Single_Bit_Adder single_bit_adder_1 (
    .a(A0), .b(xor_1_out), .Input(Control), .Carry(single_bit_adder_1_carry), .S(S0));
  Single_Bit_Adder single_bit_adder_2 (
    .a(A1), .b(xor_2_out), .Input(single_bit_adder_1_carry), .Carry(single_bit_adder_2_carry), .S(S1));
  Single_Bit_Adder single_bit_adder_3 (
    .a(A2), .b(xor_3_out), .Input(single_bit_adder_2_carry), .Carry(single_bit_adder_3_carry), .S(S2));
  Single_Bit_Adder single_bit_adder_4 (
    .a(A3), .b(xor_4_out), .Input(single_bit_adder_3_carry), .Carry(Carry_Out), .S(S3));
endmodule

module Single_Bit_Adder (
  input  Input,
  input  a,
  input  b,
  output S,
  output Carry
);

  wire and_1_out, and_2_out, xor_1_out;

  and and_1 (and_1_out, a, b);
  or or_1 (Carry, and_1_out, and_2_out);
  xor xor_1 (xor_1_out, a, b);
  and and_2 (and_2_out, xor_1_out, Input);
  xor xor_2 (S, xor_1_out, Input);
endmodule
