// Logisim project p4.circ as structural Verilog: 2 circuits, main circuit main
module main (
  input  [7:0] in_1,
  input  [7:0] in_2,
  input  Controller
);

  wire adder_1_cout;
  wire [3:0] adder_1_out, adder_1_out_2, bit_extender_1_out, bit_extender_2_out;
  wire [7:0] n2_into_1_mux_1_out_4, not_1_out;

  assign not_1_out = ~in_2;  // NOT_Gate not_1, 8 bits wide
  _2_into_1_MUX u_2_into_1_mux_1 (.in_1(in_2), .in_2(not_1_out), .in_3(Controller), .out_4(n2_into_1_mux_1_out_4));
  Adder adder_1 (
    .a(in_1), .b(n2_into_1_mux_1_out_4), .out({adder_1_out, adder_1_out_2}), .cin(Controller),
    .cout(adder_1_cout));
  Hex_Digit_Display hex_digit_display_1 (.value(bit_extender_1_out));  // open: dp
  assign bit_extender_1_out = {{3{1'b0}}, adder_1_cout};  // Bit_Extender bit_extender_1
  Hex_Digit_Display hex_digit_display_2 (.value(bit_extender_2_out));  // open: dp
  assign bit_extender_2_out = {{3{1'b0}}, adder_1_out[3]};  // Bit_Extender bit_extender_2
  Hex_Digit_Display hex_digit_display_3 (.value(adder_1_out));  // open: dp
  Hex_Digit_Display hex_digit_display_4 (.value(adder_1_out_2));  // open: dp

  // Notes on the sheet:
  //   B
  //   A
  //   Carry BIt
endmodule

module _2_into_1_MUX (
  input  [7:0] in_1,
  input  [7:0] in_2,
  input  in_3,
  output [7:0] out_4
);

  wire and_1_out, and_2_out, and_3_out, and_4_out, and_5_out, and_6_out, and_7_out, and_8_out, and_9_out,
       and_10_out, and_11_out, and_12_out, and_13_out, and_14_out, and_15_out, and_16_out, not_1_out;

  not not_1 (not_1_out, in_3);
  and and_1 (and_1_out, in_1[0], not_1_out);
  and and_2 (and_2_out, in_2[0], in_3);
  and and_3 (and_3_out, in_1[1], not_1_out);
  and and_4 (and_4_out, in_2[1], in_3);
  and and_5 (and_5_out, in_1[2], not_1_out);
  and and_6 (and_6_out, in_2[2], in_3);
  and and_7 (and_7_out, in_1[3], not_1_out);
  and and_8 (and_8_out, in_2[3], in_3);
  and and_9 (and_9_out, in_1[4], not_1_out);
  and and_10 (and_10_out, in_2[4], in_3);
  and and_11 (and_11_out, in_1[5], not_1_out);
  and and_12 (and_12_out, in_2[5], in_3);
  and and_13 (and_13_out, in_1[6], not_1_out);
  and and_14 (and_14_out, in_2[6], in_3);
  and and_15 (and_15_out, in_1[7], not_1_out);
  and and_16 (and_16_out, in_2[7], in_3);
  or or_1 (out_4[0], and_1_out, and_2_out);
  or or_2 (out_4[1], and_3_out, and_4_out);
  or or_3 (out_4[2], and_5_out, and_6_out);
  or or_4 (out_4[3], and_7_out, and_8_out);
  or or_5 (out_4[4], and_9_out, and_10_out);
  or or_6 (out_4[5], and_11_out, and_12_out);
  or or_7 (out_4[6], and_13_out, and_14_out);
  or or_8 (out_4[7], and_15_out, and_16_out);
endmodule
