// Logisim project p1.circ as structural Verilog: 3 circuits, main circuit main
module main (
  input  [2:0] X,
  input  [2:0] Y,
  output out_3,
  output out_4,
  output out_5,
  output P2,
  output out_7,
  output P4
);

  wire and_1_out, and_2_out, and_3_out, and_4_out, and_5_out, and_6_out, and_7_out, and_8_out, FA_2_out_5,
       FA_3_out_5, FA_3_sum, HA_2_carry, HA_3_carry, HA_carry, HA_sum;

  and and_1 (and_1_out, X[2], Y[2]);
  Full_Adder FA (.A(HA_carry), .B(and_1_out), .Cin(FA_2_out_5), .Sum(P4), .out_5(out_7));
  and and_2 (and_2_out, X[1], Y[2]);
  and and_3 (and_3_out, X[2], Y[1]);
  and and_4 (and_4_out, X[1], Y[1]);
  Half_Adder HA (.X(FA_3_out_5), .Y(and_3_out), .Sum(HA_sum), .Carry(HA_carry));
  Full_Adder FA_2 (.A(HA_sum), .B(and_2_out), .Cin(HA_2_carry), .Sum(out_5), .out_5(FA_2_out_5));
  and and_5 (and_5_out, X[0], Y[2]);
  and and_6 (and_6_out, X[2], Y[0]);
  Full_Adder FA_3 (.A(and_6_out), .B(and_4_out), .Cin(HA_3_carry), .Sum(FA_3_sum), .out_5(FA_3_out_5));
  Half_Adder HA_2 (.X(FA_3_sum), .Y(and_5_out), .Sum(P2), .Carry(HA_2_carry));
  and and_7 (and_7_out, X[1], Y[0]);
  and and_8 (and_8_out, X[0], Y[1]);
  Half_Adder HA_3 (.X(and_7_out), .Y(and_8_out), .Sum(out_4), .Carry(HA_3_carry));
  and and_9 (out_3, X[0], Y[0]);

  // Notes on the sheet:
  //   P5
  //   P3
  //   P1
  //   P0
endmodule

module Full_Adder (
  input  Cin,
  input  A,
  input  B,
  output Sum,
  output out_5
);

  wire and_1_out, and_2_out, xor_1_out;

  xor xor_1 (xor_1_out, A, B);
  xor xor_2 (Sum, xor_1_out, Cin);
  and and_1 (and_1_out, Cin, xor_1_out);
  and and_2 (and_2_out, B, A);
  or or_1 (out_5, and_1_out, and_2_out);

  // Notes on the sheet:
  //   Carry
endmodule

module Half_Adder (
  input  X,
  input  Y,
  output Sum,
  output Carry
);

  xor xor_1 (Sum, X, Y);
  and and_1 (Carry, X, Y);
endmodule
