// Logisim project p2.circ as structural Verilog: 3 circuits, main circuit main
module main (
  input  [7:0] in_1,
  input  [7:0] in_2,
  output out_3,
  output S14,
  output S13,
  output S12,
  output S11,
  output S10,
  output S9,
  output S8,
  output S7,
  output S6,
  output S5,
  output S4,
  output S3,
  output S2,
  output S1,
  output S0
);

  wire and_1_out, and_2_out, and_3_out, and_4_out, and_5_out, and_6_out, and_7_out, and_8_out, and_9_out,
       and_10_out, and_11_out, and_12_out, and_13_out, and_14_out, and_15_out, and_16_out, and_17_out,
       and_18_out, and_19_out, and_20_out, and_21_out, and_22_out, and_23_out, and_24_out, and_25_out,
       and_26_out, and_27_out, and_28_out, and_29_out, and_30_out, and_31_out, and_32_out, and_33_out,
       and_34_out, and_35_out, and_36_out, and_37_out, and_38_out, and_39_out, and_40_out, and_41_out,
       and_42_out, and_43_out, and_44_out, and_45_out, and_46_out, and_47_out, and_48_out, and_49_out,
       and_50_out, and_51_out, and_52_out, and_53_out, and_54_out, and_55_out, and_56_out, and_57_out,
       and_58_out, and_59_out, and_60_out, and_61_out, and_62_out, and_63_out, full_adder_2_out_5,
       full_adder_2_sum, full_adder_3_out_5, full_adder_3_sum, full_adder_4_out_5, full_adder_4_sum,
       full_adder_5_out_5, full_adder_6_out_5, full_adder_7_out_5, full_adder_7_sum, full_adder_8_out_5,
       full_adder_8_sum, full_adder_9_out_5, full_adder_9_sum, full_adder_10_out_5, full_adder_11_out_5,
       full_adder_11_sum, full_adder_12_out_5, full_adder_12_sum, full_adder_13_out_5, full_adder_13_sum,
       full_adder_14_out_5, full_adder_14_sum, full_adder_15_out_5, full_adder_16_out_5, full_adder_16_sum,
       full_adder_17_out_5, full_adder_17_sum, full_adder_18_out_5, full_adder_18_sum, full_adder_19_out_5,
       full_adder_19_sum, full_adder_20_out_5, full_adder_20_sum, full_adder_21_out_5, full_adder_22_out_5,
       full_adder_22_sum, full_adder_23_out_5, full_adder_23_sum, full_adder_24_out_5, full_adder_24_sum,
       full_adder_25_out_5, full_adder_25_sum, full_adder_26_out_5, full_adder_26_sum, full_adder_27_out_5,
       full_adder_28_out_5, full_adder_28_sum, full_adder_29_out_5, full_adder_29_sum, full_adder_30_out_5,
       full_adder_30_sum, full_adder_31_out_5, full_adder_31_sum, full_adder_32_out_5, full_adder_32_sum,
       full_adder_33_out_5, full_adder_33_sum, full_adder_34_out_5, full_adder_34_sum, full_adder_35_out_5,
       full_adder_35_sum, full_adder_36_out_5, full_adder_36_sum, full_adder_37_out_5, full_adder_37_sum,
       full_adder_38_out_5, full_adder_38_sum, full_adder_39_out_5, full_adder_39_sum, full_adder_40_out_5,
       full_adder_40_sum, full_adder_41_out_5, full_adder_41_sum, full_adder_42_out_5, full_adder_42_sum,
       full_adder_43_out_5, full_adder_43_sum, full_adder_44_out_5, full_adder_44_sum, full_adder_45_out_5,
       full_adder_45_sum, full_adder_46_out_5, full_adder_46_sum, full_adder_47_out_5, full_adder_47_sum,
       full_adder_48_out_5, full_adder_48_sum, half_adder_1_carry, half_adder_1_sum, half_adder_2_carry,
       half_adder_3_carry, half_adder_4_carry, half_adder_5_carry, half_adder_6_carry, half_adder_7_carry,
       half_adder_8_carry;

  and and_1 (and_1_out, in_2[7], in_1[7]);
  Full_Adder full_adder_1 (.out_5(out_3), .A(full_adder_3_out_5), .B(and_1_out), .Sum(S14), .Cin(full_adder_5_out_5));
  Full_Adder full_adder_2 (
    .out_5(full_adder_2_out_5), .A(full_adder_7_out_5), .B(and_5_out), .Sum(full_adder_2_sum),
    .Cin(full_adder_8_out_5));
  and and_2 (and_2_out, in_2[7], in_1[6]);
  Full_Adder full_adder_3 (
    .out_5(full_adder_3_out_5), .A(full_adder_2_out_5), .B(and_2_out), .Sum(full_adder_3_sum),
    .Cin(full_adder_4_out_5));
  Full_Adder full_adder_4 (
    .out_5(full_adder_4_out_5), .A(full_adder_2_sum), .B(and_8_out), .Sum(full_adder_4_sum),
    .Cin(full_adder_9_out_5));
  and and_3 (and_3_out, in_2[6], in_1[7]);
  Full_Adder full_adder_5 (
    .out_5(full_adder_5_out_5), .A(full_adder_3_sum), .B(and_3_out), .Sum(S13), .Cin(full_adder_6_out_5));
  Full_Adder full_adder_6 (
    .out_5(full_adder_6_out_5), .A(full_adder_4_sum), .B(and_10_out), .Sum(S12), .Cin(full_adder_10_out_5));
  and and_4 (and_4_out, in_2[7], in_1[4]);
  Full_Adder full_adder_7 (
    .out_5(full_adder_7_out_5), .A(full_adder_11_out_5), .B(and_4_out), .Sum(full_adder_7_sum),
    .Cin(full_adder_12_out_5));
  and and_5 (and_5_out, in_2[7], in_1[5]);
  and and_6 (and_6_out, in_2[6], in_1[5]);
  Full_Adder full_adder_8 (
    .out_5(full_adder_8_out_5), .A(full_adder_7_sum), .B(and_6_out), .Sum(full_adder_8_sum),
    .Cin(full_adder_13_out_5));
  and and_7 (and_7_out, in_2[5], in_1[6]);
  and and_8 (and_8_out, in_2[6], in_1[6]);
  Full_Adder full_adder_9 (
    .out_5(full_adder_9_out_5), .A(full_adder_8_sum), .B(and_7_out), .Sum(full_adder_9_sum),
    .Cin(full_adder_14_out_5));
  and and_9 (and_9_out, in_2[4], in_1[7]);
  and and_10 (and_10_out, in_2[5], in_1[7]);
  Full_Adder full_adder_10 (
    .out_5(full_adder_10_out_5), .A(full_adder_9_sum), .B(and_9_out), .Sum(S11), .Cin(full_adder_15_out_5));
  and and_11 (and_11_out, in_2[7], in_1[3]);
  Full_Adder full_adder_11 (
    .out_5(full_adder_11_out_5), .A(full_adder_16_out_5), .B(and_11_out), .Sum(full_adder_11_sum),
    .Cin(full_adder_17_out_5));
  and and_12 (and_12_out, in_2[6], in_1[4]);
  Full_Adder full_adder_12 (
    .out_5(full_adder_12_out_5), .A(full_adder_11_sum), .B(and_12_out), .Sum(full_adder_12_sum),
    .Cin(full_adder_18_out_5));
  and and_13 (and_13_out, in_2[5], in_1[5]);
  Full_Adder full_adder_13 (
    .out_5(full_adder_13_out_5), .A(full_adder_12_sum), .B(and_13_out), .Sum(full_adder_13_sum),
    .Cin(full_adder_19_out_5));
  and and_14 (and_14_out, in_2[4], in_1[6]);
  Full_Adder full_adder_14 (
    .out_5(full_adder_14_out_5), .A(full_adder_13_sum), .B(and_14_out), .Sum(full_adder_14_sum),
    .Cin(full_adder_20_out_5));
  and and_15 (and_15_out, in_2[3], in_1[7]);
  Full_Adder full_adder_15 (
    .out_5(full_adder_15_out_5), .A(full_adder_14_sum), .B(and_15_out), .Sum(S10), .Cin(full_adder_21_out_5));
  and and_16 (and_16_out, in_2[7], in_1[2]);
  Full_Adder full_adder_16 (
    .out_5(full_adder_16_out_5), .A(half_adder_1_carry), .B(and_16_out), .Sum(full_adder_16_sum),
    .Cin(full_adder_22_out_5));
  and and_17 (and_17_out, in_2[6], in_1[3]);
  Full_Adder full_adder_17 (
    .out_5(full_adder_17_out_5), .A(full_adder_16_sum), .B(and_17_out), .Sum(full_adder_17_sum),
    .Cin(full_adder_23_out_5));
  and and_18 (and_18_out, in_2[5], in_1[4]);
  Full_Adder full_adder_18 (
    .out_5(full_adder_18_out_5), .A(full_adder_17_sum), .B(and_18_out), .Sum(full_adder_18_sum),
    .Cin(full_adder_24_out_5));
  and and_19 (and_19_out, in_2[4], in_1[5]);
  Full_Adder full_adder_19 (
    .out_5(full_adder_19_out_5), .A(full_adder_18_sum), .B(and_19_out), .Sum(full_adder_19_sum),
    .Cin(full_adder_25_out_5));
  and and_20 (and_20_out, in_2[3], in_1[6]);
  Full_Adder full_adder_20 (
    .out_5(full_adder_20_out_5), .A(full_adder_19_sum), .B(and_20_out), .Sum(full_adder_20_sum),
    .Cin(full_adder_26_out_5));
  and and_21 (and_21_out, in_2[2], in_1[7]);
  Full_Adder full_adder_21 (
    .out_5(full_adder_21_out_5), .A(full_adder_20_sum), .B(and_21_out), .Sum(S9), .Cin(full_adder_27_out_5));
  and and_22 (and_22_out, in_1[1], in_2[6]);
  and and_23 (and_23_out, in_1[1], in_2[7]);
  Half_Adder half_adder_1 (.Carry(half_adder_1_carry), .X(and_23_out), .Y(full_adder_28_out_5), .Sum(half_adder_1_sum));
  and and_24 (and_24_out, in_2[6], in_1[2]);
  Full_Adder full_adder_22 (
    .out_5(full_adder_22_out_5), .A(half_adder_1_sum), .B(and_24_out), .Sum(full_adder_22_sum),
    .Cin(full_adder_29_out_5));
  and and_25 (and_25_out, in_2[5], in_1[3]);
  Full_Adder full_adder_23 (
    .out_5(full_adder_23_out_5), .A(full_adder_22_sum), .B(and_25_out), .Sum(full_adder_23_sum),
    .Cin(full_adder_30_out_5));
  and and_26 (and_26_out, in_2[4], in_1[4]);
  Full_Adder full_adder_24 (
    .out_5(full_adder_24_out_5), .A(full_adder_23_sum), .B(and_26_out), .Sum(full_adder_24_sum),
    .Cin(full_adder_31_out_5));
  and and_27 (and_27_out, in_2[3], in_1[5]);
  Full_Adder full_adder_25 (
    .out_5(full_adder_25_out_5), .A(full_adder_24_sum), .B(and_27_out), .Sum(full_adder_25_sum),
    .Cin(full_adder_32_out_5));
  and and_28 (and_28_out, in_2[2], in_1[6]);
  Full_Adder full_adder_26 (
    .out_5(full_adder_26_out_5), .A(full_adder_25_sum), .B(and_28_out), .Sum(full_adder_26_sum),
    .Cin(full_adder_33_out_5));
  and and_29 (and_29_out, in_2[1], in_1[7]);
  Full_Adder full_adder_27 (
    .out_5(full_adder_27_out_5), .A(full_adder_26_sum), .B(and_29_out), .Sum(S8), .Cin(half_adder_3_carry));
  and and_30 (and_30_out, in_1[1], in_2[5]);
  and and_31 (and_31_out, in_1[0], in_2[7]);
  Full_Adder full_adder_28 (
    .out_5(full_adder_28_out_5), .A(and_22_out), .B(and_31_out), .Sum(full_adder_28_sum),
    .Cin(full_adder_34_out_5));
  and and_32 (and_32_out, in_2[5], in_1[2]);
  Full_Adder full_adder_29 (
    .out_5(full_adder_29_out_5), .A(full_adder_28_sum), .B(and_32_out), .Sum(full_adder_29_sum),
    .Cin(full_adder_35_out_5));
  and and_33 (and_33_out, in_2[4], in_1[3]);
  Full_Adder full_adder_30 (
    .out_5(full_adder_30_out_5), .A(full_adder_29_sum), .B(and_33_out), .Sum(full_adder_30_sum),
    .Cin(full_adder_36_out_5));
  and and_34 (and_34_out, in_2[3], in_1[4]);
  Full_Adder full_adder_31 (
    .out_5(full_adder_31_out_5), .A(full_adder_30_sum), .B(and_34_out), .Sum(full_adder_31_sum),
    .Cin(full_adder_37_out_5));
  and and_35 (and_35_out, in_2[2], in_1[5]);
  Full_Adder full_adder_32 (
    .out_5(full_adder_32_out_5), .A(full_adder_31_sum), .B(and_35_out), .Sum(full_adder_32_sum),
    .Cin(full_adder_38_out_5));
  and and_36 (and_36_out, in_2[1], in_1[6]);
  Half_Adder half_adder_2 (.Carry(half_adder_2_carry), .X(full_adder_38_sum), .Y(and_45_out), .Sum(S6));
  Full_Adder full_adder_33 (
    .out_5(full_adder_33_out_5), .A(full_adder_32_sum), .B(and_36_out), .Sum(full_adder_33_sum),
    .Cin(half_adder_2_carry));
  and and_37 (and_37_out, in_2[0], in_1[7]);
  Half_Adder half_adder_3 (.Carry(half_adder_3_carry), .X(full_adder_33_sum), .Y(and_37_out), .Sum(S7));
  and and_38 (and_38_out, in_1[0], in_2[5]);
  and and_39 (and_39_out, in_1[1], in_2[4]);
  and and_40 (and_40_out, in_1[0], in_2[6]);
  Full_Adder full_adder_34 (
    .out_5(full_adder_34_out_5), .A(and_30_out), .B(and_40_out), .Sum(full_adder_34_sum),
    .Cin(full_adder_39_out_5));
  and and_41 (and_41_out, in_2[4], in_1[2]);
  Full_Adder full_adder_35 (
    .out_5(full_adder_35_out_5), .A(full_adder_34_sum), .B(and_41_out), .Sum(full_adder_35_sum),
    .Cin(full_adder_42_out_5));
  and and_42 (and_42_out, in_2[3], in_1[3]);
  Full_Adder full_adder_36 (
    .out_5(full_adder_36_out_5), .A(full_adder_35_sum), .B(and_42_out), .Sum(full_adder_36_sum),
    .Cin(full_adder_43_out_5));
  and and_43 (and_43_out, in_2[2], in_1[4]);
  Full_Adder full_adder_37 (
    .out_5(full_adder_37_out_5), .A(full_adder_36_sum), .B(and_43_out), .Sum(full_adder_37_sum),
    .Cin(full_adder_45_out_5));
  and and_44 (and_44_out, in_2[1], in_1[5]);
  Half_Adder half_adder_4 (.Carry(half_adder_4_carry), .X(full_adder_45_sum), .Y(and_51_out), .Sum(S5));
  Full_Adder full_adder_38 (
    .out_5(full_adder_38_out_5), .A(full_adder_37_sum), .B(and_44_out), .Sum(full_adder_38_sum),
    .Cin(half_adder_4_carry));
  and and_45 (and_45_out, in_2[0], in_1[6]);
  and and_46 (and_46_out, in_1[0], in_2[4]);
  and and_47 (and_47_out, in_1[1], in_2[3]);
  Full_Adder full_adder_39 (
    .out_5(full_adder_39_out_5), .A(and_39_out), .B(and_38_out), .Sum(full_adder_39_sum),
    .Cin(full_adder_40_out_5));
  Full_Adder full_adder_40 (
    .out_5(full_adder_40_out_5), .A(and_47_out), .B(and_46_out), .Sum(full_adder_40_sum),
    .Cin(full_adder_46_out_5));
  and and_48 (and_48_out, in_2[3], in_1[2]);
  Full_Adder full_adder_41 (
    .out_5(full_adder_41_out_5), .A(full_adder_40_sum), .B(and_54_out), .Sum(full_adder_41_sum),
    .Cin(full_adder_47_out_5));
  Full_Adder full_adder_42 (
    .out_5(full_adder_42_out_5), .A(full_adder_39_sum), .B(and_48_out), .Sum(full_adder_42_sum),
    .Cin(full_adder_41_out_5));
  and and_49 (and_49_out, in_2[2], in_1[3]);
  Full_Adder full_adder_43 (
    .out_5(full_adder_43_out_5), .A(full_adder_42_sum), .B(and_49_out), .Sum(full_adder_43_sum),
    .Cin(full_adder_44_out_5));
  Full_Adder full_adder_44 (
    .out_5(full_adder_44_out_5), .A(full_adder_41_sum), .B(and_57_out), .Sum(full_adder_44_sum),
    .Cin(half_adder_6_carry));
  and and_50 (and_50_out, in_2[1], in_1[4]);
  Half_Adder half_adder_5 (.Carry(half_adder_5_carry), .X(full_adder_44_sum), .Y(and_58_out), .Sum(S4));
  Full_Adder full_adder_45 (
    .out_5(full_adder_45_out_5), .A(full_adder_43_sum), .B(and_50_out), .Sum(full_adder_45_sum),
    .Cin(half_adder_5_carry));
  and and_51 (and_51_out, in_2[0], in_1[5]);
  and and_52 (and_52_out, in_1[1], in_2[2]);
  and and_53 (and_53_out, in_1[0], in_2[3]);
  Full_Adder full_adder_46 (
    .out_5(full_adder_46_out_5), .A(and_52_out), .B(and_53_out), .Sum(full_adder_46_sum),
    .Cin(full_adder_48_out_5));
  and and_54 (and_54_out, in_2[2], in_1[2]);
  and and_55 (and_55_out, in_2[1], in_1[2]);
  Full_Adder full_adder_47 (
    .out_5(full_adder_47_out_5), .A(full_adder_46_sum), .B(and_55_out), .Sum(full_adder_47_sum),
    .Cin(half_adder_7_carry));
  and and_56 (and_56_out, in_2[0], in_1[3]);
  and and_57 (and_57_out, in_2[1], in_1[3]);
  Half_Adder half_adder_6 (.Carry(half_adder_6_carry), .X(full_adder_47_sum), .Y(and_56_out), .Sum(S3));
  and and_58 (and_58_out, in_2[0], in_1[4]);
  and and_59 (and_59_out, in_1[0], in_2[2]);
  and and_60 (and_60_out, in_1[1], in_2[1]);
  Full_Adder full_adder_48 (
    .out_5(full_adder_48_out_5), .A(and_60_out), .B(and_59_out), .Sum(full_adder_48_sum),
    .Cin(half_adder_8_carry));
  and and_61 (and_61_out, in_2[0], in_1[2]);
  Half_Adder half_adder_7 (.Carry(half_adder_7_carry), .X(full_adder_48_sum), .Y(and_61_out), .Sum(S2));
  and and_62 (and_62_out, in_1[1], in_2[0]);
  and and_63 (and_63_out, in_1[0], in_2[1]);
  Half_Adder half_adder_8 (.Carry(half_adder_8_carry), .X(and_62_out), .Y(and_63_out), .Sum(S1));
  and and_64 (S0, in_2[0], in_1[0]);

  // Other names for the same wires on the sheet: X0 = in_1[0]; X1 = in_1[1]; X2 = in_1[2]; X3 = in_1[3]; X4 = in_1[4];
  //   X5 = in_1[5]; X6 = in_1[6]; X7 = in_1[7]; Y0 = in_2[0]; Y1 = in_2[1]; Y2 = in_2[2]; Y3 = in_2[3]; Y4 = in_2[4];
  //   Y5 = in_2[5]; Y6 = in_2[6]; Y7 = in_2[7]

  // Notes on the sheet:
  //   X
  //   Y
  //   S15
endmodule

// FA
module Full_Adder (
  input  A,
  input  B,
  input  Cin,
  output Sum,
  output out_5
);

  wire and_1_out, and_2_out, xor_1_out;

  xor xor_1 (xor_1_out, A, B);
  xor xor_2 (Sum, xor_1_out, Cin);
  and and_1 (and_1_out, Cin, xor_1_out);
  and and_2 (and_2_out, B, A);
  or or_1 (out_5, and_1_out, and_2_out);

  // Notes on the sheet:
  //   Carry
endmodule

// HA
module Half_Adder (
  input  X,
  input  Y,
  output Sum,
  output Carry
);

  xor xor_1 (Sum, X, Y);
  and and_1 (Carry, X, Y);
endmodule
