// Logisim project p3.circ as structural Verilog: 1 circuit, main circuit main
module main (
  input  [3:0] A,
  input  [3:0] B,
  output A___B,
  output A___B_2,
  output A___B_3
);

  wire A0_prime, A1_prime, A2_prime, A3_prime, and_1_out, and_2_out, and_3_out, and_4_out, and_5_out,
       and_6_out, and_7_out, and_8_out, and_9_out, and_10_out, and_11_out, and_12_out, and_13_out,
       and_14_out, B0_prime, B1_prime, B2_prime, B3_prime, nor_1_out, nor_2_out, nor_3_out, nor_4_out;

  not not_1 (A0_prime, A[0]);
  not not_2 (A3_prime, A[3]);
  not not_3 (B0_prime, B[0]);
  not not_4 (B3_prime, B[3]);
  not not_5 (A1_prime, A[1]);
  not not_6 (A2_prime, A[2]);
  not not_7 (B1_prime, B[1]);
  not not_8 (B2_prime, B[2]);
  and and_1 (and_1_out, A3_prime, B[3]);
  and and_2 (and_2_out, A[3], B3_prime);
  and and_3 (and_3_out, A2_prime, B[2]);
  and and_4 (and_4_out, A[2], B2_prime);
  and and_5 (and_5_out, A1_prime, B[1]);
  and and_6 (and_6_out, A[1], B1_prime);
  and and_7 (and_7_out, A0_prime, B[0]);
  and and_8 (and_8_out, A[0], B0_prime);
  nor nor_1 (nor_1_out, and_1_out, and_2_out);
  nor nor_2 (nor_2_out, and_3_out, and_4_out);
  nor nor_3 (nor_3_out, and_5_out, and_6_out);
  nor nor_4 (nor_4_out, and_7_out, and_8_out);
  and and_9 (and_9_out, nor_1_out, and_3_out);
  and and_10 (and_10_out, nor_1_out, and_4_out);
  and and_11 (and_11_out, nor_1_out, nor_2_out, and_5_out);
  and and_12 (and_12_out, nor_1_out, nor_2_out, and_6_out);
  and and_13 (and_13_out, nor_1_out, nor_2_out, nor_3_out, and_7_out);
  and and_14 (and_14_out, nor_1_out, nor_2_out, nor_3_out, and_8_out);
  and and_15 (A___B_3, nor_1_out, nor_2_out, nor_3_out, nor_4_out);
  or or_1 (A___B, and_1_out, and_9_out, and_11_out, and_13_out);
  or or_2 (A___B_2, and_2_out, and_10_out, and_12_out, and_14_out);
endmodule
