// Logisim project p4.circ as structural Verilog: 3 circuits, main circuit main
module main (
  input  [7:0] A,
  input  [7:0] B,
  output [7:0] MIN_OF_A_and_B
);

  wire n8_bit_comparator_1_out_17, n8_bit_comparator_1_out_18, n8_bit_comparator_1_out_19;

  _8_bit_comparator u_8_bit_comparator_1 (
    .A7(A[7]), .A6(A[6]), .A5(A[5]), .A4(A[4]), .A3(A[3]), .A2(A[2]), .A1(A[1]), .A0(A[0]), .B7(B[7]),
    .B6(B[6]), .B5(B[5]), .B4(B[4]), .B3(B[3]), .B2(B[2]), .B1(B[1]), .B0(B[0]),
    .out_17(n8_bit_comparator_1_out_17), .out_18(n8_bit_comparator_1_out_18),
    .out_19(n8_bit_comparator_1_out_19));
  _2X1_MUX u_2x1_mux_1 (.in_1(A), .in_2(B), .in_3(n8_bit_comparator_1_out_17), .out_4(MIN_OF_A_and_B));
endmodule

module _2X1_MUX (
  input  [7:0] in_1,
  input  [7:0] in_2,
  input  in_3,
  output [7:0] out_4
);

  wire and_1_out, and_2_out, and_3_out, and_4_out, and_5_out, and_6_out, and_7_out, and_8_out, and_9_out,
       and_10_out, and_11_out, and_12_out, and_13_out, and_14_out, and_15_out, and_16_out, not_1_out;

  not not_1 (not_1_out, in_3);
  and and_1 (and_1_out, in_1[0], not_1_out);
  and and_2 (and_2_out, in_2[0], in_3);
  and and_3 (and_3_out, in_1[1], not_1_out);
  and and_4 (and_4_out, in_2[1], in_3);
  and and_5 (and_5_out, in_1[2], not_1_out);
  and and_6 (and_6_out, in_2[2], in_3);
  and and_7 (and_7_out, in_1[3], not_1_out);
  and and_8 (and_8_out, in_2[3], in_3);
  and and_9 (and_9_out, in_1[4], not_1_out);
  and and_10 (and_10_out, in_2[4], in_3);
  and and_11 (and_11_out, in_1[5], not_1_out);
  and and_12 (and_12_out, in_2[5], in_3);
  and and_13 (and_13_out, in_1[6], not_1_out);
  and and_14 (and_14_out, in_2[6], in_3);
  and and_15 (and_15_out, in_1[7], not_1_out);
  and and_16 (and_16_out, in_2[7], in_3);
  or or_1 (out_4[0], and_1_out, and_2_out);
  or or_2 (out_4[1], and_3_out, and_4_out);
  or or_3 (out_4[2], and_5_out, and_6_out);
  or or_4 (out_4[3], and_7_out, and_8_out);
  or or_5 (out_4[4], and_9_out, and_10_out);
  or or_6 (out_4[5], and_11_out, and_12_out);
  or or_7 (out_4[6], and_13_out, and_14_out);
  or or_8 (out_4[7], and_15_out, and_16_out);
endmodule

module _8_bit_comparator (
  input  A7,
  input  A6,
  input  A5,
  input  A4,
  input  A3,
  input  A2,
  input  A1,
  input  A0,
  input  B7,
  input  B6,
  input  B5,
  input  B4,
  input  B3,
  input  B2,
  input  B1,
  input  B0,
  output out_17,
  output out_18,
  output out_19
);

  wire and_1_out, and_2_out, and_3_out, and_4_out, and_5_out, and_6_out, and_7_out, and_8_out, and_9_out,
       and_10_out, and_11_out, and_12_out, and_13_out, and_14_out, and_15_out, and_16_out, not_1_out,
       not_2_out, not_3_out, not_4_out, not_5_out, not_6_out, not_7_out, not_8_out, not_9_out, not_10_out,
       not_11_out, not_12_out, not_13_out, not_14_out, not_15_out, not_16_out, xnor_1_out, xnor_2_out,
       xnor_3_out, xnor_4_out, xnor_5_out, xnor_6_out, xnor_7_out, xnor_8_out;

  not not_1 (not_1_out, B7);
  not not_2 (not_2_out, B6);
  not not_3 (not_3_out, B5);
  not not_4 (not_4_out, B4);
  not not_5 (not_5_out, B3);
  not not_6 (not_6_out, B2);
  not not_7 (not_7_out, B1);
  not not_8 (not_8_out, B0);
  xnor xnor_1 (xnor_1_out, A7, B7);
  xnor xnor_2 (xnor_2_out, A6, B6);
  xnor xnor_3 (xnor_3_out, A5, B5);
  xnor xnor_4 (xnor_4_out, A4, B4);
  xnor xnor_5 (xnor_5_out, A3, B3);
  xnor xnor_6 (xnor_6_out, A2, B2);
  xnor xnor_7 (xnor_7_out, A1, B1);
  xnor xnor_8 (xnor_8_out, A0, B0);
  and and_1 (and_1_out, A7, not_1_out);
  and and_2 (and_2_out, A6, not_2_out, xnor_1_out);
  and and_3 (and_3_out, A5, not_3_out, xnor_1_out, xnor_2_out);
  and and_4 (and_4_out, A4, not_4_out, xnor_1_out, xnor_2_out, xnor_3_out);
  and and_5 (and_5_out, A3, not_5_out, xnor_1_out, xnor_2_out, xnor_3_out, xnor_4_out);
  and and_6 (and_6_out, A2, not_6_out, xnor_1_out, xnor_2_out, xnor_3_out, xnor_4_out, xnor_5_out);
  and and_7 (and_7_out, A1, not_7_out, xnor_1_out, xnor_2_out, xnor_3_out, xnor_4_out, xnor_5_out, xnor_6_out);
  and and_8 (and_8_out, A0, not_8_out, xnor_1_out, xnor_2_out, xnor_3_out, xnor_4_out, xnor_5_out, xnor_6_out, xnor_7_out);
  not not_9 (not_9_out, A7);
  not not_10 (not_10_out, A6);
  not not_11 (not_11_out, A5);
  not not_12 (not_12_out, A4);
  not not_13 (not_13_out, A3);
  not not_14 (not_14_out, A2);
  not not_15 (not_15_out, A1);
  not not_16 (not_16_out, A0);
  and and_9 (and_9_out, not_9_out, B7);
  and and_10 (and_10_out, not_10_out, B6, xnor_1_out);
  and and_11 (and_11_out, not_11_out, B5, xnor_1_out, xnor_2_out);
  and and_12 (and_12_out, not_12_out, B4, xnor_1_out, xnor_2_out, xnor_3_out);
  and and_13 (and_13_out, not_13_out, B3, xnor_1_out, xnor_2_out, xnor_3_out, xnor_4_out);
  and and_14 (and_14_out, not_14_out, B2, xnor_1_out, xnor_2_out, xnor_3_out, xnor_4_out, xnor_5_out);
  and and_15 (and_15_out, not_15_out, B1, xnor_1_out, xnor_2_out, xnor_3_out, xnor_4_out, xnor_5_out, xnor_6_out);
  and and_16 (and_16_out, not_16_out, B0, xnor_1_out, xnor_2_out, xnor_3_out, xnor_4_out, xnor_5_out, xnor_6_out, xnor_7_out);
  or or_1 (out_17, and_1_out, and_2_out, and_3_out, and_4_out, and_5_out, and_6_out, and_7_out, and_8_out);
  and and_17 (out_18, xnor_1_out, xnor_2_out, xnor_3_out, xnor_4_out, xnor_5_out, xnor_6_out, xnor_7_out, xnor_8_out);
  or or_2 (out_19, and_9_out, and_10_out, and_11_out, and_12_out, and_13_out, and_14_out, and_15_out, and_16_out);
endmodule
