// Logisim project 7483.circ as structural Verilog: 1 circuit, main circuit main
module main (
  input  c_in,
  input  b1,
  input  b3,
  input  b2,
  input  b0,
  input  a2,
  input  a1,
  input  a0,
  input  a3,
  output c_out,
  output s3,
  output s2,
  output s1,
  output s0
);

  wire main_2_c_out, main_3_c_out, main_4_c_out;

  One_bit_full_adder_main main_1 (.A(a3), .B(b3), .C_in(main_2_c_out), .sum(s3), .C_out(c_out));
  One_bit_full_adder_main main_2 (.A(a2), .B(b2), .C_in(main_3_c_out), .sum(s2), .C_out(main_2_c_out));
  One_bit_full_adder_main main_3 (.A(a1), .B(b1), .C_in(main_4_c_out), .sum(s1), .C_out(main_3_c_out));
  One_bit_full_adder_main main_4 (.A(a0), .B(b0), .C_in(c_in), .sum(s0), .C_out(main_4_c_out));
endmodule
