// Logisim project 8 BIT BINARY ADD_SUB.circ as structural Verilog: 1 circuit, main circuit main
module main (
  input  b7,
  input  b6,
  input  b5,
  input  b4,
  input  b3,
  input  b2,
  input  b1,
  input  b0,
  input  a7,
  input  a6,
  input  a5,
  input  a4,
  input  a3,
  input  a2,
  input  a1,
  input  a0,
  input  Control,
  output s3,
  output s7,
  output s2,
  output s6,
  output s1,
  output s5,
  output s0,
  output s4,
  output overflow
);

  wire _7483_2_c_out, _7483_c_out, xor_1_out, xor_2_out, xor_3_out, xor_4_out, xor_5_out, xor_6_out,
       xor_8_out, xor_9_out, xor_10_out, xor_11_out;

  xor xor_1 (xor_1_out, b7, a7);
  xor xor_2 (xor_2_out, b7, Control);
  xor xor_3 (xor_3_out, _7483_c_out, s7);
  xor xor_4 (xor_4_out, b6, Control);
  xor xor_5 (xor_5_out, b5, Control);
  xor xor_6 (xor_6_out, b4, Control);
  _7483_main _7483 (
    .c_out(_7483_c_out), .b3(xor_2_out), .a3(a7), .b2(xor_4_out), .a2(a6), .b1(xor_5_out), .a1(a5),
    .b0(xor_6_out), .a0(a4), .s3(s7), .s2(s6), .s1(s5), .s0(s4), .c_in(_7483_2_c_out));
  xor xor_7 (overflow, xor_3_out, xor_1_out);
  xor xor_8 (xor_8_out, b2, Control);
  xor xor_9 (xor_9_out, b3, Control);
  xor xor_10 (xor_10_out, b1, Control);
  _7483_main _7483_2 (
    .c_out(_7483_2_c_out), .b3(xor_9_out), .a3(a3), .b2(xor_8_out), .a2(a2), .b1(xor_10_out), .a1(a1),
    .b0(xor_11_out), .a0(a0), .s3(s3), .s2(s2), .s1(s1), .s0(s0), .c_in(Control));
  xor xor_11 (xor_11_out, b0, Control);

  // Notes on the sheet:
  //   for adder: give it '0' input
  //   for subtractor: give it '1' input
endmodule
