// Logisim project 8 BIT EQUAL.circ as structural Verilog: 2 circuits, main circuit main
module main (
  input  [7:0] A,
  input  [7:0] B,
  output A_B,
  output A_B_2,
  output A_B_3,
  output [7:0] out_6
);

  wire n1_bit_comparator_1_out_eq, n1_bit_comparator_1_out_gt, n1_bit_comparator_1_out_lt,
       n1_bit_comparator_2_out_eq, n1_bit_comparator_2_out_gt, n1_bit_comparator_2_out_lt,
       n1_bit_comparator_3_out_eq, n1_bit_comparator_3_out_gt, n1_bit_comparator_3_out_lt,
       n1_bit_comparator_4_out_eq, n1_bit_comparator_4_out_gt, n1_bit_comparator_4_out_lt,
       n1_bit_comparator_5_out_eq, n1_bit_comparator_5_out_gt, n1_bit_comparator_5_out_lt,
       n1_bit_comparator_6_out_eq, n1_bit_comparator_6_out_gt, n1_bit_comparator_6_out_lt,
       n1_bit_comparator_8_out_eq, n1_bit_comparator_8_out_gt, n1_bit_comparator_8_out_lt, or_1_out;

  _1_bit_comparator u_1_bit_comparator_1 (
    .in_gt(1'b0), .in_eq(1'b1), .in_lt(1'b0), .A(B[7]), .B(A[7]), .out_gt(n1_bit_comparator_1_out_gt),
    .out_eq(n1_bit_comparator_1_out_eq), .out_lt(n1_bit_comparator_1_out_lt));
  _1_bit_comparator u_1_bit_comparator_2 (
    .in_gt(n1_bit_comparator_1_out_gt), .in_eq(n1_bit_comparator_1_out_eq),
    .in_lt(n1_bit_comparator_1_out_lt), .A(B[6]), .B(A[6]), .out_gt(n1_bit_comparator_2_out_gt),
    .out_eq(n1_bit_comparator_2_out_eq), .out_lt(n1_bit_comparator_2_out_lt));
  _1_bit_comparator u_1_bit_comparator_3 (
    .in_gt(n1_bit_comparator_2_out_gt), .in_eq(n1_bit_comparator_2_out_eq),
    .in_lt(n1_bit_comparator_2_out_lt), .A(B[5]), .B(A[5]), .out_gt(n1_bit_comparator_3_out_gt),
    .out_eq(n1_bit_comparator_3_out_eq), .out_lt(n1_bit_comparator_3_out_lt));
  _1_bit_comparator u_1_bit_comparator_4 (
    .in_gt(n1_bit_comparator_3_out_gt), .in_eq(n1_bit_comparator_3_out_eq),
    .in_lt(n1_bit_comparator_3_out_lt), .A(B[4]), .B(A[4]), .out_gt(n1_bit_comparator_4_out_gt),
    .out_eq(n1_bit_comparator_4_out_eq), .out_lt(n1_bit_comparator_4_out_lt));
  _1_bit_comparator u_1_bit_comparator_5 (
    .in_gt(n1_bit_comparator_4_out_gt), .in_eq(n1_bit_comparator_4_out_eq),
    .in_lt(n1_bit_comparator_4_out_lt), .A(B[3]), .B(A[3]), .out_gt(n1_bit_comparator_5_out_gt),
    .out_eq(n1_bit_comparator_5_out_eq), .out_lt(n1_bit_comparator_5_out_lt));
  _1_bit_comparator u_1_bit_comparator_6 (
    .in_gt(n1_bit_comparator_5_out_gt), .in_eq(n1_bit_comparator_5_out_eq),
    .in_lt(n1_bit_comparator_5_out_lt), .A(B[2]), .B(A[2]), .out_gt(n1_bit_comparator_6_out_gt),
    .out_eq(n1_bit_comparator_6_out_eq), .out_lt(n1_bit_comparator_6_out_lt));
  _1_bit_comparator u_1_bit_comparator_7 (
    .in_gt(n1_bit_comparator_8_out_gt), .in_eq(n1_bit_comparator_8_out_eq),
    .in_lt(n1_bit_comparator_8_out_lt), .A(B[0]), .B(A[0]), .out_gt(A_B), .out_eq(A_B_2), .out_lt(A_B_3));
  _1_bit_comparator u_1_bit_comparator_8 (
    .in_gt(n1_bit_comparator_6_out_gt), .in_eq(n1_bit_comparator_6_out_eq),
    .in_lt(n1_bit_comparator_6_out_lt), .A(B[1]), .B(A[1]), .out_gt(n1_bit_comparator_8_out_gt),
    .out_eq(n1_bit_comparator_8_out_eq), .out_lt(n1_bit_comparator_8_out_lt));
  or or_1 (or_1_out, A_B, A_B_2);
  Multiplexer #(.width(8)) multiplexer_1 (.in0(8'h1), .in1({8{1'b0}}), .out(out_6), .sel(or_1_out));  // open: en
endmodule

module _1_bit_comparator (
  input  A,
  input  B,
  input  in_gt,
  input  in_eq,
  input  in_lt,
  output out_gt,
  output out_eq,
  output out_lt
);

  wire and_1_out, and_2_out, not_1_out, not_2_out, xnor_1_out;

  not not_1 (not_1_out, B);
  not not_2 (not_2_out, A);
  and and_1 (and_1_out, not_1_out, A, in_eq);
  and and_2 (and_2_out, B, not_2_out, in_eq);
  xnor xnor_1 (xnor_1_out, B, A);
  and and_3 (out_eq, in_eq, xnor_1_out);
  or or_1 (out_gt, in_gt, and_1_out);
  or or_2 (out_lt, and_2_out, in_lt);
endmodule
