// Logisim project p1.circ as structural Verilog: 1 circuit, main circuit main
module main (
  input  [7:0] A,
  input  [7:0] B,
  input  [2:0] in_3,
  output [7:0] \output 
);

  wire [7:0] and_1_out, binary_adder_s0, binary_subtrat_s0, func_out_6, max_out_6, min_out_6, or_1_out,
       xor_1_out;

  _8_BIT_BINARY_ADD_SUB_main binary_subtrat (
    .b7(B[7]), .b6(B[6]), .a7(A[7]), .a6(A[6]), .a5(A[5]), .b5(B[5]), .a4(A[4]), .b4(B[4]), .b3(B[3]),
    .b2(B[2]), .a3(A[3]), .a2(A[2]), .a1(A[1]), .b1(B[1]), .a0(A[0]), .b0(B[0]), .s7(binary_subtrat_s0[7]),
    .s6(binary_subtrat_s0[6]), .s5(binary_subtrat_s0[5]), .s4(binary_subtrat_s0[4]),
    .s3(binary_subtrat_s0[3]), .s2(binary_subtrat_s0[2]), .s1(binary_subtrat_s0[1]),
    .s0(binary_subtrat_s0[0]), .Control(in_3[0]));  // open: overflow
  _8_BIT_MAX_main max (.A(A), .B(B), .out_6(max_out_6));  // open: A_B, A_B_2, A_B_3
  MIN_8_BIT_main min (.A(A), .B(B), .out_6(min_out_6));  // open: A_B, A_B_2, A_B_3
  _8_BIT_EQUAL_main func (.A(A), .B(B), .out_6(func_out_6));  // open: A_B, A_B_2, A_B_3
  _8_BIT_BINARY_ADD_SUB_main binary_adder (
    .b7(B[7]), .b6(B[6]), .a7(A[7]), .a6(A[6]), .a5(A[5]), .b5(B[5]), .a4(A[4]), .b4(B[4]), .b3(B[3]),
    .b2(B[2]), .a3(A[3]), .a2(A[2]), .a1(A[1]), .b1(B[1]), .a0(A[0]), .b0(B[0]), .s7(binary_adder_s0[7]),
    .s6(binary_adder_s0[6]), .s5(binary_adder_s0[5]), .s4(binary_adder_s0[4]), .s3(binary_adder_s0[3]),
    .s2(binary_adder_s0[2]), .s1(binary_adder_s0[1]), .s0(binary_adder_s0[0]), .Control(in_3[0]));  // open: overflow
  assign and_1_out = A & B;  // AND_Gate and_1, 8 bits wide
  assign or_1_out = A | B;  // OR_Gate or_1, 8 bits wide
  assign xor_1_out = A ^ B;  // XOR_Gate xor_1, 8 bits wide
  Multiplexer #(.select(3), .width(8)) multiplexer_1 (
    .in0(binary_adder_s0), .in1(binary_subtrat_s0), .in2(and_1_out), .in3(or_1_out), .in4(xor_1_out),
    .in5(max_out_6), .in6(min_out_6), .in7(func_out_6), .out(\output ), .sel(in_3));  // open: en
  Hex_Digit_Display hex_digit_display_1 (.value(\output [7:4]));  // open: dp
  Hex_Digit_Display hex_digit_display_2 (.value(\output [3:0]));  // open: dp

  // Notes on the sheet:
  //   here func
  //   if A>B then output 00000001
  //   if A<=B then output 00000000
  //   000 A+B
  //   001 A-B
  //   010 A&B
  //   011 A|B
  //   100 A XOR B
  //   101 A>B Output:A
  //   110 A>B Output: B
  //   111 A>B Output 00000001
endmodule
