// Logisim project p0.circ as structural Verilog: 1 circuit, main circuit main
module main (
  input  in_1,
  input  in_2,
  input  in_3,
  input  Clock,
  input  Clock_2,
  input  in_6,
  input  in_7,
  input  Enable,
  input  Enable_2,
  input  Enable_3,
  input  JK_Flip_Flop,
  input  T_Flip_Flop,
  input  D_Flip_Flop,
  input  in_14,
  input  in_15,
  input  Clock_3,
  input  Enable_4,
  input  SR_Flip_Flop,
  output out_19,
  output out_20,
  output out_21,
  output out_22
);

  wire clock_1_out, clock_2_out, clock_3_out, clock_4_out;

  Clock clock_1 (.out(clock_1_out));
  J_K_Flip_Flop j_k_ff_1 (
    .J(in_1), .clk(clock_1_out), .K(in_2), .Q(out_19), .preset(Clock_2), .en(Enable), .reset(JK_Flip_Flop));  // open: Qn
  Clock u_clock_2 (.out(clock_2_out));
  Clock u_clock_3 (.out(clock_3_out));
  S_R_Flip_Flop s_r_ff_1 (
    .S(in_14), .clk(clock_2_out), .R(in_15), .Q(out_22), .preset(Clock_3), .reset(SR_Flip_Flop), .en(Enable_4));  // open: Qn
  T_Flip_Flop t_ff_1 (
    .clk(clock_3_out), .T(in_3), .Q(out_20), .preset(in_6), .reset(T_Flip_Flop), .en(Enable_2));  // open: Qn
  Clock clock_4 (.out(clock_4_out));
  D_Flip_Flop d_ff_1 (
    .clk(clock_4_out), .D(Clock), .Q(out_21), .preset(in_7), .en(Enable_3), .reset(D_Flip_Flop));  // open: Qn

  // Notes on the sheet:
  //   Clock
endmodule
