// Logisim project p1.circ as structural Verilog: 1 circuit, main circuit main
module main (
  input  Enable,
  input  Input_Bit,
  output Bit_8,
  output Bit_7,
  output Bit_6,
  output Bit_5,
  output Bit_4,
  output Bit_3,
  output Bit_2,
  output Bit_1
);

  wire Clock_out;

  Clock Clock (.out(Clock_out));
  D_Flip_Flop d_ff_1 (.clk(Clock_out), .D(Bit_7), .Q(Bit_8), .en(Enable));  // open: Qn, preset, reset
  D_Flip_Flop d_ff_2 (.clk(Clock_out), .D(Bit_6), .Q(Bit_7), .en(Enable));  // open: Qn, preset, reset
  D_Flip_Flop d_ff_3 (.clk(Clock_out), .D(Bit_5), .Q(Bit_6), .en(Enable));  // open: Qn, preset, reset
  D_Flip_Flop d_ff_4 (.clk(Clock_out), .D(Bit_4), .Q(Bit_5), .en(Enable));  // open: Qn, preset, reset
  D_Flip_Flop d_ff_5 (.clk(Clock_out), .D(Bit_3), .Q(Bit_4), .en(Enable));  // open: Qn, preset, reset
  D_Flip_Flop d_ff_6 (.clk(Clock_out), .D(Bit_2), .Q(Bit_3), .en(Enable));  // open: Qn, preset, reset
  D_Flip_Flop d_ff_7 (.clk(Clock_out), .D(Bit_1), .Q(Bit_2), .en(Enable));  // open: Qn, preset, reset
  D_Flip_Flop d_ff_8 (.clk(Clock_out), .D(Input_Bit), .Q(Bit_1), .en(Enable));  // open: Qn, preset, reset
  Hex_Digit_Display hex_digit_display_1 (.value({Bit_5, Bit_6, Bit_7, Bit_8}));  // open: dp
  Hex_Digit_Display hex_digit_display_2 (.value({Bit_1, Bit_2, Bit_3, Bit_4}));  // open: dp
endmodule
