// Logisim project p2.circ as structural Verilog: 1 circuit, main circuit main
module main (
);

  wire Clock_out;
  wire [3:0] d_ff_1_q, random_1_out;

  Clock Clock (.out(Clock_out));
  Random #(.width(4)) random_1 (.clk(Clock_out), .out(random_1_out));  // open: next, clr
  D_Flip_Flop d_ff_1 (.clk(Clock_out), .D(random_1_out[0]), .Q(d_ff_1_q[0]));  // open: Qn, preset, en, reset
  Hex_Digit_Display hex_digit_display_1 (.value(random_1_out));  // open: dp
  D_Flip_Flop d_ff_2 (.clk(Clock_out), .D(random_1_out[1]), .Q(d_ff_1_q[1]));  // open: Qn, preset, en, reset
  D_Flip_Flop d_ff_3 (.clk(Clock_out), .D(random_1_out[2]), .Q(d_ff_1_q[2]));  // open: Qn, preset, en, reset
  D_Flip_Flop d_ff_4 (.clk(Clock_out), .D(random_1_out[3]), .Q(d_ff_1_q[3]));  // open: Qn, preset, en, reset
  Hex_Digit_Display hex_digit_display_2 (.value(d_ff_1_q));  // open: dp

  // Notes on the sheet:
  //   Random Generator
  //   Bit 1 (LSB)
  //   Input Hex Display
  //   Bit 2
  //   Bit 3
  //   Bit 4 (MSB)
  //   Output Hex Display
endmodule
