// Logisim project p3.circ as structural Verilog: 1 circuit, main circuit main
module main (
  input  T,
  input  T_2,
  input  Reset,
  input  Reset_2
);

  wire Clock_2_out, Clock_out;
  wire [1:0] t_ff_5_q;
  wire [3:0] t_ff_1_q, t_ff_7_q;

  Clock Clock (.out(Clock_out));
  Hex_Digit_Display hex_digit_display_1 (.value({2'b00, t_ff_5_q}));  // open: dp
  T_Flip_Flop #(.trigger("falling")) t_ff_1 (
    .clk(Clock_out), .T(T_2), .Q(t_ff_1_q[0]), .reset(Reset_2));  // open: Qn, preset, en
  Hex_Digit_Display hex_digit_display_2 (.value(t_ff_1_q));  // open: dp
  T_Flip_Flop #(.trigger("falling")) t_ff_2 (
    .clk(t_ff_1_q[0]), .T(T_2), .Q(t_ff_1_q[1]), .reset(Reset_2));  // open: Qn, preset, en
  T_Flip_Flop #(.trigger("falling")) t_ff_3 (
    .clk(t_ff_1_q[1]), .T(T_2), .Q(t_ff_1_q[2]), .reset(Reset_2));  // open: Qn, preset, en
  T_Flip_Flop #(.trigger("falling")) t_ff_4 (
    .clk(t_ff_1_q[2]), .T(T_2), .Q(t_ff_1_q[3]), .reset(Reset_2));  // open: Qn, preset, en
  T_Flip_Flop #(.trigger("falling")) t_ff_5 (
    .clk(t_ff_1_q[3]), .T(T_2), .Q(t_ff_5_q[0]), .reset(Reset_2));  // open: Qn, preset, en
  T_Flip_Flop #(.trigger("falling")) t_ff_6 (
    .clk(t_ff_5_q[0]), .T(T_2), .Q(t_ff_5_q[1]), .reset(Reset_2));  // open: Qn, preset, en
  Clock Clock_2 (.out(Clock_2_out));
  Hex_Digit_Display hex_digit_display_3 (.value(t_ff_7_q));  // open: dp
  T_Flip_Flop #(.trigger("falling")) t_ff_7 (
    .clk(Clock_2_out), .T(T), .Q(t_ff_7_q[0]), .reset(Reset));  // open: Qn, preset, en
  T_Flip_Flop #(.trigger("falling")) t_ff_8 (
    .clk(t_ff_7_q[0]), .T(T), .Q(t_ff_7_q[1]), .reset(Reset));  // open: Qn, preset, en
  T_Flip_Flop #(.trigger("falling")) t_ff_9 (
    .clk(t_ff_7_q[1]), .T(T), .Q(t_ff_7_q[2]), .reset(Reset));  // open: Qn, preset, en
  T_Flip_Flop #(.trigger("falling")) t_ff_10 (
    .clk(t_ff_7_q[2]), .T(T), .Q(t_ff_7_q[3]), .reset(Reset));  // open: Qn, preset, en

  // Notes on the sheet:
  //   Bit 1 (LSB)
  //   6 Bit-Counter
  //   Bit 2
  //   Output in Hexadecimal (Counter from 0 to 63)
  //   Bit 3
  //   Bit 4
  //   Bit 5
  //   Bit 6 (MSB)
  //   Bit 1 (LSB)
  //   4 Bit Counter
  //   Bit 3
  //   Bit 2
  //   Bit 4
endmodule
