// Logisim project D counter.circ as structural Verilog: 1 circuit, main circuit main
module main (
  input  [1:0] C0_C1,
  input  in_2,
  output [1:0] Output
);

  wire d_ff_1_qn, d_ff_2_qn, multiplexer_1_out, multiplexer_2_out, xnor_1_out, xor_1_out;

  xnor xnor_1 (xnor_1_out, Output[0], Output[1]);
  xor xor_1 (xor_1_out, Output[0], Output[1]);
  Multiplexer #(.select(2), .enable("false")) multiplexer_1 (
    .in0(Output[1]), .in1(xor_1_out), .in2(xnor_1_out), .in3(d_ff_1_qn), .out(multiplexer_1_out), .sel(C0_C1));
  Multiplexer #(.select(2), .enable("false")) multiplexer_2 (
    .in0(Output[0]), .in1(d_ff_2_qn), .in2(d_ff_2_qn), .in3(Output[0]), .out(multiplexer_2_out), .sel(C0_C1));
  D_Flip_Flop d_ff_1 (
    .clk(in_2), .D(multiplexer_1_out), .Q(Output[1]), .Qn(d_ff_1_qn), .en(1'b1));  // open: preset, reset
  D_Flip_Flop d_ff_2 (
    .clk(in_2), .D(multiplexer_2_out), .Q(Output[0]), .Qn(d_ff_2_qn), .en(1'b1));  // open: preset, reset

  // Notes on the sheet:
  //   bit2 (MSB)
  //   bit1
endmodule
