// Logisim project JK counter.circ as structural Verilog: 1 circuit, main circuit main
module main (
  input  [1:0] C0_C1,
  input  in_2,
  output [1:0] Output
);

  wire [1:0] multiplexer_1_out, multiplexer_2_out;
  wire [1:1] Bit_1_qn;

  Multiplexer #(.select(2), .width(2), .enable("false")) multiplexer_1 (
    .in0(2'b00), .in1({2{Output[0]}}), .in2({2{Bit_1_qn[1]}}), .in3(2'b11), .out(multiplexer_1_out),
    .sel(C0_C1));
  Multiplexer #(.select(2), .width(2), .enable("false")) multiplexer_2 (
    .in0(2'b00), .in1(2'b11), .in2(2'b11), .in3(2'b00), .out(multiplexer_2_out), .sel(C0_C1));
  J_K_Flip_Flop Bit_2__MSB (
    .J(multiplexer_1_out[0]), .clk(in_2), .K(multiplexer_1_out[1]), .Q(Output[1]));  // open: Qn, preset, en, reset
  J_K_Flip_Flop Bit_1 (
    .J(multiplexer_2_out[0]), .clk(in_2), .K(multiplexer_2_out[1]), .Q(Output[0]), .Qn(Bit_1_qn[1]));  // open: preset, en, reset
endmodule
