// Logisim project Q1.circ as structural Verilog: 1 circuit, main circuit main
module main (
  input  [1:0] in_1,
  input  [1:0] in_2,
  input  [1:0] in_3,
  input  [1:0] in_4,
  output [1:0] out_5,
  output [1:0] out_6,
  output [1:0] out_7,
  output [1:0] out_8
);

  wire clock_1_out, clock_2_out, clock_3_out, clock_4_out;

  D_counter_main main_1 (.C0_C1(in_2), .in_2(clock_1_out), .Output(out_6));
  Clock clock_1 (.out(clock_1_out));
  SR_counter_main main_2 (.C0_C1(in_3), .in_2(clock_2_out), .Output(out_7));
  Clock clock_2 (.out(clock_2_out));
  T_counter_main main_3 (.C0_C1(in_4), .in_1(clock_3_out), .Output(out_8));
  Clock clock_3 (.out(clock_3_out));
  JK_counter_main main_4 (.C0_C1(in_1), .in_2(clock_4_out), .Output(out_5));
  Clock clock_4 (.out(clock_4_out));

  // Notes on the sheet:
  //   D flip flop
  //   SR flip flop
  //   T flip flop
  //   JK flip flop
endmodule
