// Logisim project Q2.circ as structural Verilog: 2 circuits, main circuit main
module main (
  input  in_1,
  input  in_2,
  input  in_3,
  input  in_4,
  input  in_5,
  input  in_6,
  input  in_7,
  input  in_8,
  input  in_9,
  input  in_10,
  input  in_11,
  input  in_12
);

  wire clock_1_out, decoderr_1_a, decoderr_1_b_2, decoderr_1_c_2, decoderr_1_d, decoderr_1_e, decoderr_1_f,
       decoderr_1_g, t_ff_1_q, t_ff_2_q, t_ff_3_q, t_ff_4_q;

  Clock clock_1 (.out(clock_1_out));
  T_Flip_Flop #(.trigger("falling")) t_ff_1 (
    .clk(clock_1_out), .T(in_1), .Q(t_ff_1_q), .reset(in_6), .en(in_5));  // open: Qn, preset
  T_Flip_Flop #(.trigger("falling")) t_ff_2 (
    .clk(t_ff_1_q), .T(in_2), .Q(t_ff_2_q), .reset(in_8), .en(in_7));  // open: Qn, preset
  T_Flip_Flop #(.trigger("falling")) t_ff_3 (
    .clk(t_ff_2_q), .T(in_3), .Q(t_ff_3_q), .reset(in_10), .en(in_9));  // open: Qn, preset
  T_Flip_Flop #(.trigger("falling")) t_ff_4 (
    .clk(t_ff_3_q), .T(in_4), .Q(t_ff_4_q), .reset(in_12), .en(in_11));  // open: Qn, preset
  decoderr decoderr_1 (
    .A__MSB(t_ff_4_q), .B(t_ff_3_q), .C(t_ff_2_q), .D__LSB(t_ff_1_q), .a(decoderr_1_a), .b_2(decoderr_1_b_2),
    .c_2(decoderr_1_c_2), .d(decoderr_1_d), .e(decoderr_1_e), .f(decoderr_1_f), .g(decoderr_1_g));
  _7_Segment_Display u_7_segment_display_1 (
    .g(decoderr_1_g), .f(decoderr_1_f), .a(decoderr_1_a), .b(decoderr_1_b_2), .e(decoderr_1_e),
    .d(decoderr_1_d), .c(decoderr_1_c_2));  // open: dp

  // Notes on the sheet:
  //   4bit Asynchronous counter
endmodule

module decoderr (
  input  A__MSB,
  input  B,
  input  C,
  input  D__LSB,
  output a,
  output b_2,
  output c_2,
  output d,
  output e,
  output f,
  output g
);

  wire and_1_out, and_2_out, and_3_out, and_4_out, and_5_out, and_6_out, and_7_out, and_8_out, and_9_out,
       and_10_out, and_11_out, and_12_out, and_13_out, and_14_out, and_15_out, and_16_out, and_17_out,
       and_18_out, and_19_out, and_20_out, and_21_out, and_22_out, and_23_out, and_24_out, and_25_out,
       and_26_out, and_27_out, and_28_out, and_29_out, and_30_out, and_31_out, and_32_out, not_1_out,
       not_2_out, not_3_out, not_4_out;

  not not_1 (not_1_out, A__MSB);
  not not_2 (not_2_out, C);
  not not_3 (not_3_out, B);
  not not_4 (not_4_out, D__LSB);
  and and_1 (and_1_out, not_3_out, not_4_out);
  and and_2 (and_2_out, not_1_out, C);
  and and_3 (and_3_out, B, C);
  and and_4 (and_4_out, A__MSB, not_4_out);
  and and_5 (and_5_out, not_1_out, B, D__LSB);
  and and_6 (and_6_out, A__MSB, not_3_out, not_2_out);
  and and_7 (and_7_out, not_1_out, not_3_out);
  and and_8 (and_8_out, not_1_out, not_2_out, not_4_out);
  and and_9 (and_9_out, not_1_out, C, D__LSB);
  and and_10 (and_10_out, A__MSB, not_2_out, D__LSB);
  and and_11 (and_11_out, not_1_out, not_2_out);
  and and_12 (and_12_out, not_1_out, D__LSB);
  and and_13 (and_13_out, not_2_out, D__LSB);
  and and_14 (and_14_out, not_1_out, B);
  and and_15 (and_15_out, A__MSB, not_3_out);
  and and_16 (and_16_out, not_3_out, not_4_out);
  and and_17 (and_17_out, not_3_out, C);
  and and_18 (and_18_out, C, not_4_out);
  and and_19 (and_19_out, A__MSB, not_2_out);
  and and_20 (and_20_out, B, not_2_out, D__LSB);
  and and_21 (and_21_out, A__MSB, C);
  and and_22 (and_22_out, A__MSB, B);
  and and_23 (and_23_out, not_2_out, not_4_out);
  and and_24 (and_24_out, B, not_4_out);
  and and_25 (and_25_out, not_1_out, B, not_2_out);
  and and_26 (and_26_out, A__MSB, not_3_out, not_2_out);
  and and_27 (and_27_out, A__MSB, C, D__LSB);
  and and_28 (and_28_out, not_3_out, C);
  and and_29 (and_29_out, C, not_4_out);
  and and_30 (and_30_out, A__MSB, not_3_out);
  and and_31 (and_31_out, A__MSB, D__LSB);
  and and_32 (and_32_out, not_1_out, B, not_2_out);
  or or_1 (a, and_1_out, and_2_out, and_3_out, and_4_out, and_5_out, and_6_out);
  or or_2 (b_2, and_7_out, and_1_out, and_8_out, and_9_out, and_10_out);
  or or_3 (c_2, and_11_out, and_12_out, and_13_out, and_14_out, and_15_out);
  or or_4 (d, and_16_out, and_17_out, and_18_out, and_19_out, and_20_out);
  or or_5 (e, and_16_out, and_18_out, and_21_out, and_22_out);
  or or_6 (f, and_23_out, and_24_out, and_25_out, and_26_out, and_27_out);
  or or_7 (g, and_28_out, and_29_out, and_30_out, and_31_out, and_32_out);
endmodule
