// Logisim project Q3.circ as structural Verilog: 1 circuit, main circuit main
module main (
  input  [7:0] A,
  input  Shift__1____Load__0,
  input  [7:0] B,
  input  Clear_All,
  output Carry,
  output [7:0] Y__Sum
);

  wire adder_1_cout, adder_1_out, Clock_out, not_1_out, shift_register_1_out, shift_register_2_out;

  not not_1 (not_1_out, Shift__1____Load__0);
  Shift_Register shift_register_1 (
    .shift(Shift__1____Load__0), .in(1'b0), .clk(Clock_out), .out(shift_register_1_out), .load(not_1_out),
    .clr(Clear_All), .d0(A[7]), .d1(A[6]), .d2(A[5]), .d3(A[4]), .d4(A[3]), .d5(A[2]), .d6(A[1]), .d7(A[0]));  // open: q0, q1, q2, q3, q4, q5, q6, q7
  Shift_Register shift_register_2 (
    .shift(Shift__1____Load__0), .in(1'b0), .clk(Clock_out), .out(shift_register_2_out), .load(not_1_out),
    .clr(Clear_All), .d0(B[7]), .d1(B[6]), .d2(B[5]), .d3(B[4]), .d4(B[3]), .d5(B[2]), .d6(B[1]), .d7(B[0]));  // open: q0, q1, q2, q3, q4, q5, q6, q7
  Clock Clock (.out(Clock_out));
  Adder #(.width(1)) adder_1 (
    .a(shift_register_1_out), .b(shift_register_2_out), .out(adder_1_out), .cin(Carry), .cout(adder_1_cout));
  Shift_Register #(.length(1)) shift_register_3 (
    .shift(Shift__1____Load__0), .in(adder_1_cout), .clk(Clock_out), .out(Carry), .clr(Clear_All));  // open: load, d0, q0
  Shift_Register shift_register_4 (
    .shift(Shift__1____Load__0), .in(adder_1_out), .clk(Clock_out), .clr(Clear_All), .q0(Y__Sum[7]),
    .q1(Y__Sum[6]), .q2(Y__Sum[5]), .q3(Y__Sum[4]), .q4(Y__Sum[3]), .q5(Y__Sum[2]), .q6(Y__Sum[1]),
    .q7(Y__Sum[0]));  // open: out, load, d0, d1, d2, d3, d4, d5, d6, d7

  // Notes on the sheet:
  //   8 Bit Adder using only Shift Registers and a Full Adder
endmodule
