// Logisim project SR counter.circ as structural Verilog: 1 circuit, main circuit main
module main (
  input  [1:0] C0_C1,
  input  in_2,
  output [1:0] Output
);

  wire [0:0] Bit_1_qn, Bit_2__MSB_qn;
  wire [1:0] and_2_out, and_4_out, multiplexer_1_out, multiplexer_2_out;

  and and_1 (and_2_out[1], Bit_1_qn[0], Output[1]);
  and and_2 (and_2_out[0], Bit_2__MSB_qn[0], Bit_1_qn[0]);
  and and_3 (and_4_out[1], Output[1], Output[0]);
  and and_4 (and_4_out[0], Bit_2__MSB_qn[0], Output[0]);
  Multiplexer #(.select(2), .width(2), .enable("false")) multiplexer_1 (
    .in0(2'b00), .in1(and_4_out), .in2(and_2_out), .in3({Output[1], Bit_2__MSB_qn[0]}),
    .out(multiplexer_1_out), .sel(C0_C1));
  Multiplexer #(.select(2), .width(2), .enable("false")) multiplexer_2 (
    .in0(2'b00), .in1({Output[0], Bit_1_qn[0]}), .in2({Output[0], Bit_1_qn[0]}), .in3(2'b00),
    .out(multiplexer_2_out), .sel(C0_C1));
  S_R_Flip_Flop Bit_2__MSB (
    .S(multiplexer_1_out[0]), .clk(in_2), .R(multiplexer_1_out[1]), .Q(Output[1]), .Qn(Bit_2__MSB_qn[0]));  // open: preset, reset, en
  S_R_Flip_Flop Bit_1 (
    .S(multiplexer_2_out[0]), .clk(in_2), .R(multiplexer_2_out[1]), .Q(Output[0]), .Qn(Bit_1_qn[0]));  // open: preset, reset, en
endmodule
