// Logisim project T counter.circ as structural Verilog: 1 circuit, main circuit main
module main (
  input  in_1,
  input  [1:0] C0_C1,
  output [1:0] Output
);

  wire Bit_1_qn, multiplexer_1_out, multiplexer_2_out;

  Multiplexer #(.select(2), .enable("false")) multiplexer_1 (
    .in0(1'b0), .in1(Output[0]), .in2(Bit_1_qn), .in3(1'b1), .out(multiplexer_1_out), .sel(C0_C1));
  Multiplexer #(.select(2), .enable("false")) multiplexer_2 (
    .in0(1'b0), .in1(1'b1), .in2(1'b1), .in3(1'b0), .out(multiplexer_2_out), .sel(C0_C1));
  T_Flip_Flop Bit_2__MSB (.clk(in_1), .T(multiplexer_1_out), .Q(Output[1]));  // open: Qn, preset, reset, en
  T_Flip_Flop Bit_1 (.clk(in_1), .T(multiplexer_2_out), .Q(Output[0]), .Qn(Bit_1_qn));  // open: preset, reset, en
endmodule
