// Logisim project p1.circ as structural Verilog: 1 circuit, main circuit main
module main (
  input  [1:0] in_1,
  output [1:0] out_2
);

  wire clock_1_out;
  wire [1:0] multiplexer_1_out, multiplexer_2_out, multiplexer_3_out, multiplexer_4_out;

  Multiplexer #(.select(2), .width(2), .enable("false")) multiplexer_1 (
    .in0(2'b01), .in1(2'b10), .in2(2'b11), .in3(2'b00), .out(multiplexer_1_out), .sel(out_2));
  Multiplexer #(.select(2), .width(2), .enable("false")) multiplexer_2 (
    .in0(2'b11), .in1(2'b00), .in2(2'b01), .in3(2'b10), .out(multiplexer_2_out), .sel(out_2));
  Multiplexer #(.select(2), .width(2), .enable("false")) multiplexer_3 (
    .in0(2'b10), .in1(2'b11), .in2(2'b00), .in3(2'b01), .out(multiplexer_3_out), .sel(out_2));
  Clock clock_1 (.out(clock_1_out));
  Multiplexer #(.select(2), .width(2), .disabled(0), .enable("false")) multiplexer_4 (
    .in0(out_2), .in1(multiplexer_1_out), .in2(multiplexer_2_out), .in3(multiplexer_3_out),
    .out(multiplexer_4_out), .sel(in_1));
  Register #(.width(2)) register_1 (.D(multiplexer_4_out), .Q(out_2), .clk(clock_1_out));  // open: en, clr

  // Other names for the same wires on the sheet: C1C0[1:0] = in_1
endmodule
