// Logisim project p2.circ as structural Verilog: 1 circuit, main circuit main
module main (
  input  [15:0] in_1,
  input  [15:0] in_2,
  input  [15:0] in_3,
  output [31:0] out_4
);

  wire clock_1_out;
  wire [15:0] register_1_q, register_2_q, register_3_q;
  wire [31:0] adder_1_out, multiplier_1_out, register_4_q, register_5_q;

  Clock clock_1 (.out(clock_1_out));
  Register #(.width(16)) register_1 (.D(in_1), .Q(register_1_q), .clk(clock_1_out));  // open: en, clr
  Register #(.width(16)) register_2 (.D(in_2), .Q(register_2_q), .clk(clock_1_out));  // open: en, clr
  Register #(.width(16)) register_3 (.D(in_3), .Q(register_3_q), .clk(clock_1_out));  // open: en, clr
  Register #(.width(32)) register_4 (.D(multiplier_1_out), .Q(register_4_q), .clk(clock_1_out));  // open: en, clr
  Multiplier #(.width(32)) multiplier_1 (
    .a({{16{1'b0}}, register_1_q}), .b({{16{1'b0}}, register_2_q}), .out(multiplier_1_out));  // open: cin, cout
  Register #(.width(32)) register_5 (
    .D({{16{1'b0}}, register_3_q}), .Q(register_5_q), .clk(clock_1_out));  // open: en, clr
  Adder #(.width(32)) adder_1 (.a(register_4_q), .b(register_5_q), .out(adder_1_out));  // open: cin, cout
  Register #(.width(32)) register_6 (.D(adder_1_out), .Q(out_4), .clk(clock_1_out));  // open: en, clr
endmodule
