// Logisim project p3.circ as structural Verilog: 1 circuit, main circuit main
module main (
  input  in_1,
  output _0100,
  output _1001,
  output out_4,
  output _1011
);

  wire _1S0, _1S0_C, _1S1, _1S1_C, _2S0, _2S0_C, _2S1, _2S1_C, _3S0, _3S0_C, _3S1, _3S1_C, A_C, and_1_out,
       and_2_out, and_3_out, and_4_out, and_5_out, and_6_out, and_7_out, clock_1_out, or_1_out, or_2_out,
       or_3_out, or_4_out;

  not not_1 (A_C, in_1);
  and and_1 (and_1_out, _2S1, _2S0_C);
  or or_1 (or_1_out, and_1_out, in_1);
  and and_2 (and_2_out, _1S1_C, _1S0, in_1);
  and and_3 (and_3_out, _1S1, _1S0_C, A_C);
  and and_4 (and_4_out, _2S1_C, _2S0, A_C);
  and and_5 (and_5_out, _2S1, _2S0_C, A_C);
  and and_6 (and_6_out, _3S1, _3S0_C, in_1);
  and and_7 (and_7_out, _3S0, A_C);
  or or_2 (or_2_out, and_2_out, and_3_out);
  or or_3 (or_3_out, and_4_out, and_5_out);
  or or_4 (or_4_out, and_6_out, and_7_out);
  Clock clock_1 (.out(clock_1_out));
  D_Flip_Flop d_ff_1 (.clk(clock_1_out), .D(or_2_out), .Q(_1S1), .Qn(_1S1_C));  // open: preset, en, reset
  D_Flip_Flop d_ff_2 (.clk(clock_1_out), .D(A_C), .Q(_1S0), .Qn(_1S0_C));  // open: preset, en, reset
  D_Flip_Flop d_ff_3 (.clk(clock_1_out), .D(or_3_out), .Q(_2S1), .Qn(_2S1_C));  // open: preset, en, reset
  D_Flip_Flop d_ff_4 (.clk(clock_1_out), .D(or_1_out), .Q(_2S0), .Qn(_2S0_C));  // open: preset, en, reset
  D_Flip_Flop d_ff_5 (.clk(clock_1_out), .D(or_4_out), .Q(_3S1), .Qn(_3S1_C));  // open: preset, en, reset
  D_Flip_Flop d_ff_6 (.clk(clock_1_out), .D(in_1), .Q(_3S0), .Qn(_3S0_C));  // open: preset, en, reset
  and and_8 (_0100, _1S1, _1S0, A_C);
  and and_9 (_1001, _2S1, _2S0, in_1);
  and and_10 (_1011, _3S1, _3S0, in_1);
  or or_5 (out_4, _0100, _1001, _1011);

  // Other names for the same wires on the sheet: A = in_1
endmodule
