// Logisim project 1901CS65_A2.circ as structural Verilog: 2 circuits, main circuit main
module main (
  input  [7:0] Intensity_Input__From_Sensor,
  input  in_2,
  input  Reset,
  output [2:0] Direction_of_Movement
);

  wire and_1_out, and_2_out, and_3_out, and_4_out, and_5_out, and_6_out, and_7_out, and_8_out, and_9_out,
       Clock_out, demultiplexer_1_out0, demultiplexer_1_out1, demultiplexer_1_out2, demultiplexer_1_out3,
       demultiplexer_1_out4, demultiplexer_1_out5, intensity_input_x_1_x, not_1_out, not_2_out, not_3_out,
       not_4_out, or_1_out, or_2_out, or_3_out;

  Clock Clock (.out(Clock_out));
  Intensity_Input__x intensity_input_x_1 (
    .in_1(Intensity_Input__From_Sensor), .Clock(Clock_out), .Reset(Reset), .x(intensity_input_x_1_x));
  not not_1 (not_1_out, intensity_input_x_1_x);
  and and_1 (and_1_out, not_4_out, not_1_out);
  and and_2 (and_2_out, not_2_out, Direction_of_Movement[0], intensity_input_x_1_x);
  and and_3 (and_3_out, not_3_out, Direction_of_Movement[0], intensity_input_x_1_x);
  and and_4 (and_4_out, Direction_of_Movement[0], not_1_out, not_3_out, not_2_out);
  and and_5 (and_5_out, Direction_of_Movement[1], not_4_out);
  and and_6 (and_6_out, Direction_of_Movement[1], intensity_input_x_1_x);
  and and_7 (and_7_out, Direction_of_Movement[1], Direction_of_Movement[0], not_1_out);
  and and_8 (and_8_out, Direction_of_Movement[2], not_4_out);
  and and_9 (and_9_out, Direction_of_Movement[2], intensity_input_x_1_x);
  or or_1 (or_1_out, and_1_out, and_2_out, and_3_out);
  or or_2 (or_2_out, and_4_out, and_5_out, and_6_out);
  or or_3 (or_3_out, and_7_out, and_8_out, and_9_out);
  D_Flip_Flop D2 (.clk(Clock_out), .D(or_3_out), .Q(Direction_of_Movement[2]), .reset(Reset));  // open: Qn, preset, en
  not not_2 (not_2_out, Direction_of_Movement[2]);
  not not_3 (not_3_out, Direction_of_Movement[1]);
  not not_4 (not_4_out, Direction_of_Movement[0]);
  D_Flip_Flop D1 (.clk(Clock_out), .D(or_2_out), .Q(Direction_of_Movement[1]), .reset(Reset));  // open: Qn, preset, en
  D_Flip_Flop D0 (.clk(Clock_out), .D(or_1_out), .Q(Direction_of_Movement[0]), .reset(Reset));  // open: Qn, preset, en
  Demultiplexer #(.select(3)) demultiplexer_1 (
    .out0(demultiplexer_1_out0), .out1(demultiplexer_1_out1), .out2(demultiplexer_1_out2),
    .out3(demultiplexer_1_out3), .out4(demultiplexer_1_out4), .out5(demultiplexer_1_out5), .in(in_2),
    .sel(Direction_of_Movement));  // open: out6, out7, en
  LED Right (.in(demultiplexer_1_out0));
  LED Left (.in(demultiplexer_1_out1));
  LED Up (.in(demultiplexer_1_out2));
  LED Down (.in(demultiplexer_1_out3));
  LED Front (.in(demultiplexer_1_out4));
  LED Back (.in(demultiplexer_1_out5));

  // Notes on the sheet:
  //   Intensity to X
  //   The Finite State Machine Logic
endmodule

// X
module Intensity_Input__x (
  input  [7:0] in_1,
  input  Clock,
  input  Reset,
  output x
);

  wire [7:0] register_1_q;

  Comparator comparator_1 (.a(in_1), .b(register_1_q), .gt(x));  // open: eq, lt
  Register register_1 (.D(in_1), .Q(register_1_q), .clk(Clock), .clr(Reset));  // open: en

  // Notes on the sheet:
  //   Intenity Input from sensor
  //   Register
endmodule
