// Logisim project 1901Cs65_A3.circ as structural Verilog: 2 circuits, main circuit main
module main (
  input  Input_1,
  input  Input_0,
  input  [1:0] Address,
  input  Write_read,
  output Ouput_1,
  output Output_0
);

  wire binary_cell_bc_1_output, binary_cell_bc_2_output, binary_cell_bc_3_output, binary_cell_bc_4_output,
       binary_cell_bc_5_output, binary_cell_bc_6_output, binary_cell_bc_7_output, binary_cell_bc_8_output,
       demultiplexer_1_out0, demultiplexer_1_out1, demultiplexer_1_out2, demultiplexer_1_out3;

  Demultiplexer #(.select(2)) demultiplexer_1 (
    .out0(demultiplexer_1_out0), .out1(demultiplexer_1_out1), .out2(demultiplexer_1_out2),
    .out3(demultiplexer_1_out3), .in(1'b1), .sel(Address));  // open: en
  Binary_Cell__BC binary_cell_bc_1 (
    .Input(Input_1), .Select(demultiplexer_1_out0), .Write_Read(Write_read), .Output(binary_cell_bc_1_output));
  Binary_Cell__BC binary_cell_bc_2 (
    .Input(Input_1), .Select(demultiplexer_1_out1), .Write_Read(Write_read), .Output(binary_cell_bc_2_output));
  Binary_Cell__BC binary_cell_bc_3 (
    .Input(Input_1), .Select(demultiplexer_1_out2), .Write_Read(Write_read), .Output(binary_cell_bc_3_output));
  Binary_Cell__BC binary_cell_bc_4 (
    .Input(Input_1), .Select(demultiplexer_1_out3), .Write_Read(Write_read), .Output(binary_cell_bc_4_output));
  or or_1 (Ouput_1, binary_cell_bc_4_output, binary_cell_bc_3_output, binary_cell_bc_2_output, binary_cell_bc_1_output);
  Binary_Cell__BC binary_cell_bc_5 (
    .Input(Input_0), .Select(demultiplexer_1_out0), .Write_Read(Write_read), .Output(binary_cell_bc_5_output));
  Binary_Cell__BC binary_cell_bc_6 (
    .Input(Input_0), .Select(demultiplexer_1_out1), .Write_Read(Write_read), .Output(binary_cell_bc_6_output));
  Binary_Cell__BC binary_cell_bc_7 (
    .Input(Input_0), .Select(demultiplexer_1_out2), .Write_Read(Write_read), .Output(binary_cell_bc_7_output));
  Binary_Cell__BC binary_cell_bc_8 (
    .Input(Input_0), .Select(demultiplexer_1_out3), .Write_Read(Write_read), .Output(binary_cell_bc_8_output));
  or or_2 (Output_0, binary_cell_bc_8_output, binary_cell_bc_7_output, binary_cell_bc_6_output, binary_cell_bc_5_output);

  // Notes on the sheet:
  //   Write/Read = "1" for writing
  //   "0" for reading
  //   INPUTS
  //   OUTPUTS
  //   SRAM
  //   4 x 2 RAM Memory
  //   Initially as no value is stored in the circuit,
  //   Therefore it is showing error, it will work once values are stored
endmodule

// BC
module Binary_Cell__BC (
  input  Select,
  input  Input,
  input  Write_Read,
  output Output
);

  wire and_1_out, and_2_out, not_1_out, not_2_out, not_3_out, not_4_out, or_1_out, or_2_out;

  not not_1 (not_1_out, Input);
  and and_1 (and_1_out, Select, not_1_out, Write_Read);
  and and_2 (and_2_out, Select, Input, Write_Read);
  or or_1 (or_1_out, and_1_out, not_3_out);
  or or_2 (or_2_out, not_2_out, and_2_out);
  not not_2 (not_2_out, or_1_out);
  not not_3 (not_3_out, or_2_out);
  not not_4 (not_4_out, Write_Read);
  and and_3 (Output, Select, not_2_out, not_4_out);

  // Notes on the sheet:
  //   A Binary Cell (BC) for RAM Memory
  //   The Basic Unit which is repeated and araanged to make RAM memory
  //   Write/Read = "1" for writing
  //   "0" for reading
endmodule
