// Logisim project 1901Cs65_Ass7.circ as structural Verilog: 1 circuit, main circuit main
module main (
  input  [3:0] M,
  input  [3:0] Q,
  output [7:0] out_3
);

  wire clock_1_out, multiplexer_1_out, multiplexer_5_out, multiplexer_6_out, register_1_q, Reset_out;
  wire [0:0] Q_1_q;
  wire [2:0] counter_1_q;
  wire [3:0] adder_1_out, multiplexer_2_out, multiplexer_3_out, multiplexer_4_out, subtractor_1_out;

  Button Reset (.out(Reset_out));
  // Probe on M
  Adder #(.width(4)) adder_1 (.a(out_3[7:4]), .b(M), .out(adder_1_out));  // open: cin, cout
  Subtractor #(.width(4)) subtractor_1 (.a(out_3[7:4]), .b(M), .out(subtractor_1_out));  // open: bin, bout
  Multiplexer multiplexer_1 (.in0(1'b1), .in1(register_1_q), .out(multiplexer_1_out), .sel(register_1_q));  // open: en
  Multiplexer #(.select(2), .width(4)) multiplexer_2 (
    .in0(out_3[7:4]), .in1(adder_1_out), .in2(subtractor_1_out), .in3(out_3[7:4]), .out(multiplexer_2_out),
    .sel({out_3[0], Q_1_q[0]}));  // open: en
  Register #(.width(1)) register_1 (
    .D(multiplexer_1_out), .Q(register_1_q), .clk(clock_1_out), .clr(Reset_out));  // open: en
  // Probe on Q
  Multiplexer #(.width(4)) multiplexer_3 (
    .in0(4'b0000), .in1({{2{multiplexer_2_out[3]}}, multiplexer_2_out[2:1]}), .out(multiplexer_3_out),
    .sel(register_1_q));  // open: en
  Multiplexer #(.width(4)) multiplexer_4 (
    .in0(Q), .in1({multiplexer_2_out[0], out_3[3:1]}), .out(multiplexer_4_out), .sel(register_1_q));  // open: en
  Multiplexer multiplexer_5 (.in0(1'b0), .in1(out_3[0]), .out(multiplexer_5_out), .sel(register_1_q));  // open: en
  Clock clock_1 (.out(clock_1_out));
  Register #(.width(4)) A (.D(multiplexer_3_out), .Q(out_3[7:4]), .clk(clock_1_out));  // open: en, clr
  Register #(.width(4)) u_Q (.D(multiplexer_4_out), .Q(out_3[3:0]), .clk(clock_1_out));  // open: en, clr
  Register #(.width(1)) Q_1 (.D(multiplexer_5_out), .Q(Q_1_q[0]), .clk(clock_1_out));  // open: en, clr
  Counter #(.width(3), .max('h7)) counter_1 (
    .Q(counter_1_q), .clk(clock_1_out), .clr(Reset_out));  // open: load, D, count, carry
  LED led_1 (.in(multiplexer_6_out));
  Multiplexer #(.select(3)) multiplexer_6 (
    .in0(1'b0), .in1(1'b0), .in2(1'b0), .in3(1'b0), .in4(1'b0), .in5(1'b1), .in7(1'b0),
    .out(multiplexer_6_out), .sel(counter_1_q));  // open: in6, en
  // Probe on out_3

  // Notes on the sheet:
  //   11 Right Shift
  //   MULTIPLICAND
  //   00 Right Shift
  //   01 First A + M Then Right Shift 
  //   10 First A - M Then Right Shift
  //   MULTIPLIER
  //   THE 4-BIT MUlTIPLIER USING BOOTH'S MULTIPLICATION APPROACH
  //   and keep ticking the clock until the led changes to blue
  //   After pressing the resetting button set the values for multiplier and multiplicand
  //   CLOCK
  //   ANSWER
  //   No of operations
endmodule
