// Logisim project 1901CS65_ESE_Cs322.circ as structural Verilog: 2 circuits, main circuit main
module main (
  input  [7:0] A,
  input  Shift__1____Load__0,
  input  [7:0] B,
  input  Clear_All,
  output Carry,
  output [7:0] Y__Sum
);

  wire Clock_out, full_adder_1_out_4, full_adder_1_out_5, not_1_out, shift_register_1_out,
       shift_register_2_out;

  Clock Clock (.out(Clock_out));
  not not_1 (not_1_out, Shift__1____Load__0);
  Shift_Register shift_register_1 (
    .shift(Shift__1____Load__0), .in(1'b0), .clk(Clock_out), .out(shift_register_1_out), .load(not_1_out),
    .clr(Clear_All), .d0(A[7]), .d1(A[6]), .d2(A[5]), .d3(A[4]), .d4(A[3]), .d5(A[2]), .d6(A[1]), .d7(A[0]));  // open: q0, q1, q2, q3, q4, q5, q6, q7
  Shift_Register shift_register_2 (
    .shift(Shift__1____Load__0), .in(1'b0), .clk(Clock_out), .out(shift_register_2_out), .load(not_1_out),
    .clr(Clear_All), .d0(B[7]), .d1(B[6]), .d2(B[5]), .d3(B[4]), .d4(B[3]), .d5(B[2]), .d6(B[1]), .d7(B[0]));  // open: q0, q1, q2, q3, q4, q5, q6, q7
  Full_Adder full_adder_1 (
    .in_1(shift_register_1_out), .in_2(shift_register_2_out), .in_3(Carry), .out_4(full_adder_1_out_4),
    .out_5(full_adder_1_out_5));
  Shift_Register #(.length(1)) shift_register_3 (
    .shift(Shift__1____Load__0), .in(full_adder_1_out_5), .clk(Clock_out), .out(Carry), .clr(Clear_All));  // open: load, d0, q0
  Shift_Register shift_register_4 (
    .shift(Shift__1____Load__0), .in(full_adder_1_out_4), .clk(Clock_out), .clr(Clear_All), .q0(Y__Sum[7]),
    .q1(Y__Sum[6]), .q2(Y__Sum[5]), .q3(Y__Sum[4]), .q4(Y__Sum[3]), .q5(Y__Sum[2]), .q6(Y__Sum[1]),
    .q7(Y__Sum[0]));  // open: out, load, d0, d1, d2, d3, d4, d5, d6, d7

  // Notes on the sheet:
  //   Shift Register
  //   Shift Register
  //   8 Bit Serial Adder using a single Full Adder
  //   Full Adder
  //   Shift Register
  //   To Run first set load to 0 and put values in registers and tick clock once 
  //   Then set load to 1 and tick clock 8 times and you will have your answer and carry value
endmodule

module Full_Adder (
  input  in_1,
  input  in_2,
  input  in_3,
  output out_4,
  output out_5
);

  wire and_1_out, and_2_out, xor_1_out;

  and and_1 (and_1_out, in_1, in_2);
  xor xor_1 (xor_1_out, in_1, in_2);
  and and_2 (and_2_out, in_3, xor_1_out);
  xor xor_2 (out_4, xor_1_out, in_3);
  or or_1 (out_5, and_2_out, and_1_out);
endmodule
