// Logisim project ALU.circ as structural Verilog: 5 circuits, main circuit ALU
module ALU (
  input  [7:0] A,
  input  [7:0] B,
  input  [1:0] Operation,
  output [7:0] Result
);

  wire [7:0] multiplexer_1_out, n8_bit_adder_subtracter_1_result, n8_bit_and_1_result, n8_bit_xor_1_result;

  _8_bit_AND u_8_bit_and_1 (.Result(n8_bit_and_1_result), .A(A), .B(B));
  _8_bit_xor u_8_bit_xor_1 (.Result(n8_bit_xor_1_result), .A(A), .B(B));
  _8_bit_Adder_Subtracter u_8_bit_adder_subtracter_1 (
    .Add_Sub_Control(Operation[0]), .Result(n8_bit_adder_subtracter_1_result), .A(A), .B(B));
  Multiplexer #(.width(8), .enable("false")) multiplexer_1 (
    .in0(n8_bit_and_1_result), .in1(n8_bit_xor_1_result), .out(multiplexer_1_out), .sel(Operation[0]));
  Multiplexer #(.width(8), .enable("false")) multiplexer_2 (
    .in0(multiplexer_1_out), .in1(n8_bit_adder_subtracter_1_result), .out(Result), .sel(Operation[1]));

  // Notes on the sheet:
  //   AND
  //   xor
  //   +/-
  //   Full 8-bit ALU
endmodule

module _8_bit_AND (
  input  [7:0] A,
  input  [7:0] B,
  output [7:0] Result
);

  and AND (Result[0], A[0], B[0]);
  and AND_2 (Result[1], A[1], B[1]);
  and AND_3 (Result[2], A[2], B[2]);
  and AND_4 (Result[3], A[3], B[3]);
  and AND_5 (Result[4], A[4], B[4]);
  and AND_6 (Result[5], A[5], B[5]);
  and AND_7 (Result[6], A[6], B[6]);
  and AND_8 (Result[7], A[7], B[7]);

  // Notes on the sheet:
  //   8-bit AND
endmodule

module _8_bit_xor (
  input  [7:0] A,
  input  [7:0] B,
  output [7:0] Result
);

  xor xor_1 (Result[0], A[0], B[0]);
  xor xor_2 (Result[1], A[1], B[1]);
  xor xor_3 (Result[2], A[2], B[2]);
  xor xor_4 (Result[3], A[3], B[3]);
  xor xor_5 (Result[4], A[4], B[4]);
  xor xor_6 (Result[5], A[5], B[5]);
  xor xor_7 (Result[6], A[6], B[6]);
  xor xor_8 (Result[7], A[7], B[7]);

  // Notes on the sheet:
  //   8-bit xor
endmodule

module _8_bit_Adder_Subtracter (
  input  Add_Sub_Control,
  input  [7:0] A,
  input  [7:0] B,
  output [7:0] Result
);

  wire n1_bit_adder_1_carry_out, n1_bit_adder_2_carry_out, n1_bit_adder_3_carry_out,
       n1_bit_adder_4_carry_out, n1_bit_adder_5_carry_out, n1_bit_adder_6_carry_out,
       n1_bit_adder_7_carry_out, xor_1_out, xor_2_out, xor_3_out, xor_4_out, xor_5_out, xor_6_out, xor_7_out,
       xor_8_out;

  xor xor_1 (xor_1_out, Add_Sub_Control, B[0]);
  xor xor_2 (xor_2_out, Add_Sub_Control, B[1]);
  xor xor_3 (xor_3_out, Add_Sub_Control, B[2]);
  xor xor_4 (xor_4_out, Add_Sub_Control, B[3]);
  xor xor_5 (xor_5_out, Add_Sub_Control, B[4]);
  xor xor_6 (xor_6_out, Add_Sub_Control, B[5]);
  xor xor_7 (xor_7_out, Add_Sub_Control, B[6]);
  xor xor_8 (xor_8_out, Add_Sub_Control, B[7]);
  _1_bit_Adder u_1_bit_adder_1 (
    .A(A[0]), .B(xor_1_out), .Result(Result[0]), .Carry_Out(n1_bit_adder_1_carry_out),
    .Carry_In(Add_Sub_Control));
  _1_bit_Adder u_1_bit_adder_2 (
    .A(A[1]), .B(xor_2_out), .Result(Result[1]), .Carry_Out(n1_bit_adder_2_carry_out),
    .Carry_In(n1_bit_adder_1_carry_out));
  _1_bit_Adder u_1_bit_adder_3 (
    .A(A[2]), .B(xor_3_out), .Result(Result[2]), .Carry_Out(n1_bit_adder_3_carry_out),
    .Carry_In(n1_bit_adder_2_carry_out));
  _1_bit_Adder u_1_bit_adder_4 (
    .A(A[3]), .B(xor_4_out), .Result(Result[3]), .Carry_Out(n1_bit_adder_4_carry_out),
    .Carry_In(n1_bit_adder_3_carry_out));
  _1_bit_Adder u_1_bit_adder_5 (
    .A(A[4]), .B(xor_5_out), .Result(Result[4]), .Carry_Out(n1_bit_adder_5_carry_out),
    .Carry_In(n1_bit_adder_4_carry_out));
  _1_bit_Adder u_1_bit_adder_6 (
    .A(A[5]), .B(xor_6_out), .Result(Result[5]), .Carry_Out(n1_bit_adder_6_carry_out),
    .Carry_In(n1_bit_adder_5_carry_out));
  _1_bit_Adder u_1_bit_adder_7 (
    .A(A[6]), .B(xor_7_out), .Result(Result[6]), .Carry_Out(n1_bit_adder_7_carry_out),
    .Carry_In(n1_bit_adder_6_carry_out));
  _1_bit_Adder u_1_bit_adder_8 (
    .A(A[7]), .B(xor_8_out), .Result(Result[7]), .Carry_In(n1_bit_adder_7_carry_out));  // open: Carry_Out

  // Notes on the sheet:
  //   8-bit Adder/Subtractor
endmodule

// +
module _1_bit_Adder (
  input  Carry_In,
  input  A,
  input  B,
  output Result,
  output Carry_Out
);

  wire and_1_out, and_2_out, xor_1_out;

  and and_1 (and_1_out, A, B);
  xor xor_1 (xor_1_out, A, B);
  or or_1 (Carry_Out, and_1_out, and_2_out);
  and and_2 (and_2_out, Carry_In, xor_1_out);
  xor xor_2 (Result, Carry_In, xor_1_out);

  // Notes on the sheet:
  //   Full Adder
endmodule
